// Logisim project 思考题1.circ as structural Verilog: 6 circuits, main circuit main
module main (
  input  CLK,
  input  [3:0] X,
  input  [3:0] Y,
  input  Reset,
  output [7:0] Prod
);

  wire comparator_2_eq, LOAD, STOP;
  wire [0:0] adder4b_1_f;
  wire [3:0] \_4位同步计数器_q0 , adder4b_1_cout, counter_1_q, multiplexer_1_out, multiplexer_2_out;

  // Probe on nothing
  // Probe on nothing
  Multiplexer #(.width(4), .enable("false")) multiplexer_1 (
    .in0(4'b0000), .in1(X), .out(multiplexer_1_out), .sel(Prod[0]));
  Hex_Digit_Display hex_digit_display_1 (.value(X));  // open: dp
  ADDER4b adder4b_1 (
    .X(multiplexer_1_out), .Y(Prod[7:4]), .F({adder4b_1_cout[2:0], adder4b_1_f[0]}),
    .Cout(adder4b_1_cout[3]), .Cin(1'b0));
  Hex_Digit_Display hex_digit_display_2 (.value(Y));  // open: dp
  Register #(.width(4), .Select("low")) register_1 (
    .D(adder4b_1_cout), .en(STOP), .Q(Prod[7:4]), .clk(CLK), .clr(Reset));
  Hex_Digit_Display hex_digit_display_3 (.value(Prod[7:4]));  // open: dp
  Hex_Digit_Display hex_digit_display_4 (.value(Prod[3:0]));  // open: dp
  Register #(.width(4), .Select("low")) Y_2 (.D(multiplexer_2_out), .en(STOP), .Q(Prod[3:0]), .clk(CLK), .clr(Reset));
  Multiplexer #(.width(4), .enable("false")) multiplexer_2 (
    .in0({adder4b_1_f[0], Prod[3:1]}), .in1(Y), .out(multiplexer_2_out), .sel(LOAD));
  // Probe on X
  // Probe on Y
  // Probe on Prod
  CNTR4U \_4位同步计数器  (
    .CLK(CLK), .LD(1'b0), .CLR(Reset), .Q0(\_4位同步计数器_q0 [0]), .Q1(\_4位同步计数器_q0 [1]), .D0(1'b0), .D1(1'b0),
    .D2(1'b0), .Q2(\_4位同步计数器_q0 [2]), .Q3(\_4位同步计数器_q0 [3]), .D3(1'b0), .ENP(1'b1), .ENT(1'b1));  // open: RCO
  Counter #(.width(4), .max('h5), .ongoal("stay")) counter_1 (
    .Q(counter_1_q), .clk(CLK), .clr(Reset));  // open: load, D, count, carry, preset, down
  Comparator #(.width(4)) comparator_1 (.a(\_4位同步计数器_q0 ), .b(4'b0000), .eq(LOAD));  // open: gt, lt
  Comparator #(.width(4)) comparator_2 (.a(\_4位同步计数器_q0 ), .b(4'b0101), .eq(comparator_2_eq));  // open: gt, lt
  not not_1 (STOP, comparator_2_eq);

  // Other names for the same wires on the sheet: Z[7:0] = Prod; RST = Reset

  // Notes on the sheet:
  //   X
  //   输入引脚
  //   P
  //   =
  //   请勿修改引脚名称、电路名称及电路封装外观
  //   提示: 采用无符号数一位乘法实现4位二进制乘法器，禁止直接使用乘法器组件
  //   ×
  //   =
  //   输出引脚
endmodule

module CNTR4U (
  input  CLK,
  input  LD,
  input  CLR,
  input  D0,
  input  D1,
  input  D2,
  input  D3,
  input  ENP,
  input  ENT,
  output Q0,
  output Q1,
  output Q2,
  output Q3,
  output RCO
);

  lab3_1_CNTR4U cntr4u_1 (
    .CLK(CLK), .LD(LD), .CLR(CLR), .Q0(Q0), .Q1(Q1), .D0(D0), .D1(D1), .D2(D2), .Q2(Q2), .Q3(Q3), .D3(D3),
    .ENP(ENP), .ENT(ENT), .RCO(RCO));

  // Notes on the sheet:
  //   输入引脚
  //   请勿修改引脚名称、电路名称及电路封装外观
  //   提示：使用独立逻辑门实现4位二进制同步计数器，禁止直接使用计数器组件。
  //   输出引脚
endmodule

module ADDER4b (
  input  [3:0] X,
  input  [3:0] Y,
  input  Cin,
  output [3:0] F,
  output Cout
);

  wire fa_1_cout, fa_2_cout, fa_3_cout;
  wire [3:0] bit_extender_1_out, xor_1_out;

  assign bit_extender_1_out = {{3{Cin}}, Cin};  // Bit_Extender bit_extender_1
  Hex_Digit_Display hex_digit_display_1 (.value(X), .dp(1'b0));
  assign xor_1_out = bit_extender_1_out ^ Y;  // XOR_Gate xor_1, 4 bits wide
  Hex_Digit_Display hex_digit_display_2 (.value(xor_1_out), .dp(1'b0));
  FA fa_1 (.A(X[0]), .B(xor_1_out[0]), .Cin(Cin), .F(F[0]), .Cout(fa_1_cout));
  Hex_Digit_Display hex_digit_display_3 (.value(F), .dp(1'b0));
  FA fa_2 (.A(X[1]), .B(xor_1_out[1]), .Cin(fa_1_cout), .F(F[1]), .Cout(fa_2_cout));
  FA fa_3 (.A(X[2]), .B(xor_1_out[2]), .Cin(fa_2_cout), .F(F[2]), .Cout(fa_3_cout));
  FA fa_4 (.A(X[3]), .B(xor_1_out[3]), .Cin(fa_3_cout), .F(F[3]), .Cout(Cout));

  // Other names for the same wires on the sheet: SUM[3:0] = F; 操作数x[3:0] = X; 操作数y[3:0] = Y

  // Notes on the sheet:
  //   输入引脚
  //   +
  //   =
  //   请勿修改引脚名称、电路名称及电路封装外观
  //   提示：使用独立逻辑门及全加器FA子电路实现4位二进制数加减法器，禁止直接使用加减法器组件。
  //   输出引脚
endmodule

module FA (
  input  A,
  input  B,
  input  Cin,
  output F,
  output Cout
);

  wire and_1_out, and_2_out, and_3_out;

  xor xor_1 (F, A, B, Cin);
  and and_1 (and_1_out, A, B);
  and and_2 (and_2_out, B, Cin);
  and and_3 (and_3_out, A, Cin);
  or or_1 (Cout, and_1_out, and_2_out, and_3_out);

  // Notes on the sheet:
  //   全加器
endmodule

module BarrelSFT8b (
  input  [7:0] DataIn,
  input  [2:0] shamt,
  input  IN,
  input  L_R,
  input  A_L,
  output [7:0] DataOut
);

  Multiplexer #(.select(2), .width(8), .enable("false")) multiplexer_1 ();  // open: in0, in1, in2, in3, out, sel
  Multiplexer #(.select(2), .width(8), .enable("false")) multiplexer_2 ();  // open: in0, in1, in2, in3, out, sel
  Multiplexer #(.select(2), .width(8), .enable("false")) multiplexer_3 (.out(DataOut));  // open: in0, in1, in2, in3, sel

  // Other names for the same wires on the sheet: Arth_Logic = A_L; Din[7:0] = DataIn; Dout[7:0] = DataOut; Input = IN;
  //   Left_Right = L_R

  // Notes on the sheet:
  //   L/R,A/L: 00逻辑右移，01算术右移，10逻辑左移，11：循环左移
  //   输入引脚
  //   请勿修改引脚名称、电路名称及电路封装外观
  //   提示：使用多路选择器级联实现8位桶形移位器，禁止直接使用移位器组件。
  //   输出引脚
endmodule

module \_8位乘法器  (
  input  clk,
  input  rst,
  input  [7:0] x,
  input  [7:0] y,
  input  [15:0] in_5
);

  wire [7:0] main_1_prod, main_2_prod, main_3_prod, main_4_prod;
  wire [15:0] adder_1_out, adder_2_out, bit_extender_1_out, bit_extender_2_out, bit_extender_3_out,
       bit_extender_4_out, shifter_1_out, shifter_2_out, shifter_3_out;

  main main_1 (.CLK(clk), .X(x[3:0]), .Y(y[3:0]), .Prod(main_1_prod), .Reset(rst));
  main main_2 (.CLK(clk), .X(x[7:4]), .Y(y[3:0]), .Prod(main_2_prod), .Reset(rst));
  main main_3 (.CLK(clk), .X(x[3:0]), .Y(y[7:4]), .Prod(main_3_prod), .Reset(rst));
  main main_4 (.CLK(clk), .X(x[7:4]), .Y(y[7:4]), .Prod(main_4_prod), .Reset(rst));
  assign bit_extender_1_out = {{8{1'b0}}, main_1_prod};  // Bit_Extender bit_extender_1
  assign bit_extender_2_out = {{8{1'b0}}, main_2_prod};  // Bit_Extender bit_extender_2
  assign bit_extender_3_out = {{8{1'b0}}, main_3_prod};  // Bit_Extender bit_extender_3
  assign bit_extender_4_out = {{8{1'b0}}, main_4_prod};  // Bit_Extender bit_extender_4
  Shifter #(.width(16)) shifter_1 (.in(bit_extender_2_out), .\dist (4'b0100), .out(shifter_1_out));
  Shifter #(.width(16)) shifter_2 (.in(bit_extender_3_out), .\dist (4'b0100), .out(shifter_2_out));
  Shifter #(.width(16)) shifter_3 (.in(bit_extender_4_out), .\dist (4'b1000), .out(shifter_3_out));
  Adder #(.width(16)) adder_1 (.a(bit_extender_1_out), .b(shifter_1_out), .out(adder_1_out));  // open: cin, cout
  Adder #(.width(16)) adder_2 (.a(adder_1_out), .b(shifter_2_out), .out(adder_2_out));  // open: cin, cout
  Adder #(.width(16)) adder_3 (.a(adder_2_out), .b(shifter_3_out), .out(in_5));  // open: cin, cout
endmodule
