// Logisim project lab5.2.circ as structural Verilog: 1 circuit, main circuit DataRam
// DataRAM
module DataRam (
  input  CLK,
  input  CLR,
  input  WE,
  input  [2:0] MemOp,
  input  [17:0] Addr,
  input  [31:0] Din,
  output AlignErr,
  output [31:0] DataOut
);

  wire and_3_out, and_4_out, and_5_out, and_6_out, and_7_out, and_8_out, and_9_out, and_10_out, and_11_out,
       and_12_out, and_13_out, or_1_out, or_2_out, or_3_out, or_4_out, or_5_out, or_6_out, or_7_out;
  wire [1:0] and_2_out;
  wire [7:0] multiplexer_1_out, multiplexer_2_out, multiplexer_3_out, multiplexer_5_out, ram_3_data,
       ram_4_data;
  wire [15:0] multiplexer_4_out, ram_1_data;
  wire [31:0] bit_extender_1_out, bit_extender_2_out, bit_extender_3_out, bit_extender_4_out;

  and and_1 (and_2_out[1], ~MemOp[0], ~MemOp[1], ~MemOp[2]);  // AND_Gate
  and and_2 (and_2_out[0], ~MemOp[0], MemOp[1], MemOp[2]);  // AND_Gate
  and and_3 (and_3_out, MemOp[0], ~MemOp[1], MemOp[2]);  // AND_Gate
  Multiplexer #(.width(8), .enable("false")) multiplexer_1 (
    .in0(Din[7:0]), .in1(Din[15:8]), .out(multiplexer_1_out), .sel(or_2_out));
  RAM #(.addrWidth(18), .bus("separate"), .Select("high")) ram_1 (
    .addr({Addr[17:2], 2'b00}), .din(Din[7:0]), .data(ram_1_data[7:0]), .str(and_13_out), .sel(or_4_out),
    .clk(CLK), .ld(or_4_out), .clr(CLR));
  RAM #(.addrWidth(18), .bus("separate"), .Select("high")) ram_2 (
    .addr({Addr[17:2], 2'b00}), .din(multiplexer_1_out), .data(ram_1_data[15:8]), .str(and_13_out),
    .sel(or_5_out), .clk(CLK), .ld(or_5_out), .clr(CLR));
  or or_1 (or_1_out, and_2_out[1], and_2_out[0], and_3_out);
  Multiplexer #(.width(8), .enable("false")) multiplexer_2 (
    .in0(Din[7:0]), .in1(Din[23:16]), .out(multiplexer_2_out), .sel(and_2_out[1]));
  and and_4 (and_4_out, ~Addr[0], ~MemOp[0], MemOp[1]);  // AND_Gate
  and and_5 (and_5_out, MemOp[0], ~MemOp[1]);  // AND_Gate
  or or_2 (or_2_out, and_2_out[1], and_2_out[0]);
  and and_6 (and_6_out, ~Addr[0], ~Addr[1], ~MemOp[2], ~MemOp[0], ~MemOp[1]);  // AND_Gate
  and and_7 (and_7_out, ~Addr[0], ~Addr[1], MemOp[0], ~MemOp[1]);  // AND_Gate
  and and_8 (and_8_out, Addr[0], ~Addr[1], MemOp[0], ~MemOp[1]);  // AND_Gate
  and and_9 (and_9_out, ~Addr[0], Addr[1], MemOp[0], ~MemOp[1]);  // AND_Gate
  and and_10 (and_10_out, Addr[0], Addr[1], MemOp[0], ~MemOp[1]);  // AND_Gate
  and and_11 (and_11_out, ~Addr[0], ~Addr[1], ~MemOp[0], MemOp[1]);  // AND_Gate
  and and_12 (and_12_out, ~Addr[0], Addr[1], ~MemOp[0], MemOp[1]);  // AND_Gate
  RAM #(.addrWidth(18), .bus("separate"), .Select("high")) ram_3 (
    .addr({Addr[17:2], 2'b00}), .din(multiplexer_2_out), .data(ram_3_data), .str(and_13_out), .sel(or_6_out),
    .clk(CLK), .ld(or_6_out), .clr(CLR));
  Multiplexer #(.select(2), .width(8), .enable("false")) multiplexer_3 (
    .in0(Din[7:0]), .in1(Din[15:8]), .in2(Din[31:24]), .out(multiplexer_3_out), .sel(and_2_out));  // open: in3
  not not_1 (AlignErr, or_3_out);
  or or_3 (or_3_out, and_4_out, and_5_out, and_6_out);
  or or_4 (or_4_out, and_6_out, and_7_out, and_11_out);
  or or_5 (or_5_out, and_6_out, and_8_out, and_11_out);
  or or_6 (or_6_out, and_6_out, and_9_out, and_12_out);
  or or_7 (or_7_out, and_6_out, and_10_out, and_12_out);
  and and_13 (and_13_out, or_1_out, WE);
  RAM #(.addrWidth(18), .bus("separate"), .Select("high")) ram_4 (
    .addr({Addr[17:2], 2'b00}), .din(multiplexer_3_out), .data(ram_4_data), .str(and_13_out), .sel(or_7_out),
    .clk(CLK), .ld(or_7_out), .clr(CLR));
  Multiplexer #(.width(16), .enable("false")) multiplexer_4 (
    .in0(ram_1_data), .in1({ram_4_data, ram_3_data}), .out(multiplexer_4_out), .sel(Addr[1]));
  Multiplexer #(.select(2), .width(8), .enable("false")) multiplexer_5 (
    .in0(ram_1_data[7:0]), .in1(ram_1_data[15:8]), .in2(ram_3_data), .in3(ram_4_data),
    .out(multiplexer_5_out), .sel(Addr[1:0]));
  assign bit_extender_1_out = {{16{1'b0}}, multiplexer_4_out};  // Bit_Extender bit_extender_1
  assign bit_extender_2_out = {{16{multiplexer_4_out[15]}}, multiplexer_4_out};  // Bit_Extender bit_extender_2
  assign bit_extender_3_out = {{24{1'b0}}, multiplexer_5_out};  // Bit_Extender bit_extender_3
  assign bit_extender_4_out = {{24{multiplexer_5_out[7]}}, multiplexer_5_out};  // Bit_Extender bit_extender_4
  Multiplexer #(.select(3), .width(32), .enable("false")) multiplexer_6 (
    .in0({ram_4_data, ram_3_data, ram_1_data}), .in1(bit_extender_3_out), .in2(bit_extender_1_out),
    .in5(bit_extender_4_out), .in6(bit_extender_2_out), .out(DataOut), .sel(MemOp));  // open: in3, in4, in7

  // Other names for the same wires on the sheet: Dout[31:0] = DataOut

  // Notes on the sheet:
  //   输入引脚
  //   请勿修改引脚名称、电路名称及电路封装外观
  //   为了后续实验中的引用，不要修改MemOp的编码定义、引脚名称和在布局中的位置。
  //   32位数据存储器，按字节分4片存储，可按照字节、半字和字进行存储；读取字节或半字时，支持0扩展和符号位扩展。
  //   输出引脚
endmodule
