// Logisim project lab5.5.circ as structural Verilog: 15 circuits, main circuit main
module main (
  input  [2:0] ExtOp,
  input  [2:0] MemOp,
  input  RegWr,
  input  ALUASrc,
  input  MemWr,
  input  [1:0] ALUBSrc,
  input  [31:0] Initial_Address,
  input  [3:0] ALUctr,
  input  MemtoReg,
  input  [2:0] BandJ,
  input  clk,
  input  ReSet,
  output [31:0] PC,
  output [31:0] BusW,
  output [31:0] Din,
  output NPCASrc,
  output NPCBSrc
);

  wire alu_1_zero;
  wire [13:0] alu_1_s_2;
  wire [17:0] alu_1_s;
  wire [31:0] dataram_1_dataout, idu_1_busa, idu_1_dataa, idu_1_datab, idu_1_imm, rom_1_data;

  IFU ifu_1 (
    .CLK(clk), .Reset(ReSet), .NxtASrc(NPCASrc), .NxtBSrc(NPCBSrc), .Initial_Address(Initial_Address),
    .Imm(idu_1_imm), .BusA(idu_1_busa), .PC(PC));
  ROM #(.addrWidth(16), .dataWidth(32), .Select("high")) rom_1 (.addr(PC[17:2]), .data(rom_1_data), .sel(1'b1));
  // Probe on PC
  // Probe on idu_1_imm
  lab5_4_IDU idu_1 (
    .ExtOp(ExtOp), .RegWr(RegWr), .ALUASrc(ALUASrc), .ALUBSrc(ALUBSrc), .IR(rom_1_data), .BusW(BusW),
    .PC(PC), .DataA(idu_1_dataa), .BusB(Din), .DataB(idu_1_datab), .Imm(idu_1_imm), .BusA(idu_1_busa),
    .CLK(clk));  // open: OpCode, Funct3, Funct7
  // Probe on Din
  // Probe on BusW
  lab4_5_ALU alu_1 (.A(idu_1_dataa), .B(idu_1_datab), .ALUctr(ALUctr), .S({alu_1_s_2, alu_1_s}), .Zero(alu_1_zero));
  BandJ bandj_1 (.Branch(BandJ), .NxtASrc(NPCASrc), .Zero(alu_1_zero), .NxtBSrc(NPCBSrc), .Result0(alu_1_s[0]));
  DataRam dataram_1 (
    .Addr(alu_1_s), .Din(Din), .DataOut(dataram_1_dataout), .CLK(clk), .CLR(ReSet), .MemOp(MemOp), .WE(MemWr));  // open: AlignErr
  Multiplexer #(.width(32), .enable("false")) multiplexer_1 (
    .in0({alu_1_s_2, alu_1_s}), .in1(dataram_1_dataout), .out(BusW), .sel(MemtoReg));

  // Other names for the same wires on the sheet: Init_Addr[31:0] = Initial_Address

  // Notes on the sheet:
  //   ALUASrc: pull=down
  //   NPCASrc: pull=down
  //   ExtOp: pull=down
  //   ALUBSrc: pull=down
  //   RegWr: pull=down
  //   ALUctr: pull=down
  //   BandJ: pull=down
  //   NPCBSrc: pull=down
  //   输入信号
  //   请勿修改引脚名称、电路名称及电路封装外观
  //   为了后续实验中的引用，不要修改控制信号的编码定义、引脚名称和在布局中的位置。
  //   指令存储器和数据存储器数据位都是32位，指令存储器编址以字为单位，数据存储器编址以字节为单位。
  //   32位数据存储器，按字节分4片存储，可按照字节、半字和字进行存储；读取字节或半字时，支持0扩展和符号位扩展。
  //   contents of rom_1 (hex, n*v repeats v):
  //   256*0 fedca2b7 f9c28293 1006013 6502223 6400303 6601423 6405383 6701623 4042d413 6444b3 649533
  //   8505b3 b2a633 b2b6b3 40b287b3 6f02823 67c263 67d263 40086f 4808e7 1917
  //   输出信号
endmodule

module BandJ (
  input  [2:0] Branch,
  input  Zero,
  input  Result0,
  output NxtASrc,
  output NxtBSrc
);

  wire not_1_out, or_1_out;

  not not_1 (not_1_out, Zero);
  or or_1 (or_1_out, Zero, ~Result0);  // OR_Gate
  Multiplexer #(.select(3), .enable("false")) multiplexer_1 (
    .in0(1'b0), .in1(1'b1), .in2(1'b1), .in4(Zero), .in5(not_1_out), .in6(Result0), .in7(or_1_out),
    .out(NxtBSrc), .sel(Branch));  // open: in3
  and and_1 (NxtASrc, ~Branch[0], Branch[1], ~Branch[2]);  // AND_Gate

  // Notes on the sheet:
  //   Zero: pull=down
  //   Branch: pull=down
  //   输入信号
  //   请勿修改引脚名称、电路名称及电路封装外观
  //   不要修改控制信号的编码定义、引脚名称和在布局中的位置。
  //   输出信号
endmodule

module IFU (
  input  [31:0] Initial_Address,
  input  [31:0] Imm,
  input  [31:0] BusA,
  input  CLK,
  input  Reset,
  input  NxtASrc,
  input  NxtBSrc,
  output [31:0] PC
);

  wire not_1_out;
  wire [31:0] adder_1_out, multiplexer_1_out, multiplexer_2_out, multiplexer_3_out;

  Multiplexer #(.width(32), .enable("false")) multiplexer_1 (
    .in0(PC), .in1(BusA), .out(multiplexer_1_out), .sel(NxtASrc));
  Multiplexer #(.width(32), .enable("false")) multiplexer_2 (
    .in0(32'h4), .in1(Imm), .out(multiplexer_2_out), .sel(NxtBSrc));
  Adder #(.width(32)) adder_1 (.a(multiplexer_1_out), .b(multiplexer_2_out), .out(adder_1_out));  // open: cin, cout
  Multiplexer #(.width(32), .enable("false")) multiplexer_3 (
    .in0(Initial_Address), .in1(adder_1_out), .out(multiplexer_3_out), .sel(not_1_out));
  not not_1 (not_1_out, Reset);
  Register #(.width(32), .Select("high")) register_1 (
    .D(multiplexer_3_out), .en(1'b1), .Q(PC), .clk(CLK));  // open: clr

  // Other names for the same wires on the sheet: Init_Addr[31:0] = Initial_Address

  // Notes on the sheet:
  //   BusA: pull=down
  //   NxtASrc: pull=down
  //   Imm: pull=down
  //   NxtBSrc: pull=down
  //   输入信号
  //   请勿修改引脚名称、电路名称及电路封装外观
  //   指令存储器256KB，数据位为32位，地址位为16位。PC寄存器数据宽度32位，片选信号高电平有效
  //   输出信号
endmodule

module IDU (
  input  [31:0] IR,
  input  [31:0] BusW,
  input  [31:0] PC,
  input  [2:0] ExtOp,
  input  RegWr,
  input  ALUASrc,
  input  [1:0] ALUBSrc,
  input  CLK,
  output [31:0] DataA,
  output [31:0] DataB,
  output [31:0] BusA,
  output [31:0] BusB,
  output [6:0] OpCode,
  output [31:0] Imm,
  output [2:0] Funct3,
  output [6:0] Funct7
);

  \lab5_4_立即数扩展器  \u_立即数扩展器_1  (.Instr(IR), .Extop(ExtOp), .imm(Imm));
  lab5_4_RegFile regfile_1 (
    .R1_num(IR[19:15]), .R2_num(IR[24:20]), .Write_Reg_num(IR[11:7]), .Din(BusW), .Reg1Out(BusA),
    .Reg2Out(BusB), .Write_Enable(RegWr), .Clock(CLK));
  Multiplexer #(.width(32), .enable("false")) multiplexer_1 (.in0(BusA), .in1(PC), .out(DataA), .sel(ALUASrc));
  Multiplexer #(.select(2), .width(32), .enable("false")) multiplexer_2 (
    .in0(BusB), .in1(32'h4), .in2(Imm), .out(DataB), .sel(ALUBSrc));  // open: in3

  assign Funct3 = IR[14:12];
  assign Funct7 = IR[31:25];
  assign OpCode = IR[6:0];

  // Other names for the same wires on the sheet: op[6:0] = IR[6:0]

  // Notes on the sheet:
  //   ALUASrc: pull=down
  //   BusW: pull=down
  //   PC: pull=down
  //   RegWr: pull=down
  //   ExtOp: pull=down
  //   ALUBSrc: pull=down
  //   输入信号
  //   为了后续实验中的引用，不要修改ALUASrc、ALUBSrc和EXtOP编码定义。
  //   请勿修改引脚名称、电路名称及电路封装外观
  //   输出信号
  //   修改寄存器堆电路设计，0号寄存器始终为0。
endmodule

module RegFile (
  input  [4:0] R1_num,
  input  [4:0] R2_num,
  input  [4:0] Write_Reg_num,
  input  [31:0] Din,
  input  Write_Enable,
  input  Clock,
  output [31:0] Reg1Out,
  output [31:0] Reg2Out
);

  wire and_1_out, and_2_out, and_3_out, and_4_out, and_5_out, and_6_out, and_7_out, and_8_out, and_9_out,
       and_10_out, and_11_out, and_12_out, and_13_out, and_14_out, and_15_out, and_16_out, and_17_out,
       and_18_out, and_19_out, and_20_out, and_21_out, and_22_out, and_23_out, and_24_out, and_25_out,
       and_26_out, and_27_out, and_28_out, and_29_out, and_30_out, and_31_out, and_32_out, decoder_1_out0,
       decoder_1_out1, decoder_1_out2, decoder_1_out3, decoder_1_out4, decoder_1_out5, decoder_1_out6,
       decoder_1_out7, decoder_1_out8, decoder_1_out9, decoder_1_out10, decoder_1_out11, decoder_1_out12,
       decoder_1_out13, decoder_1_out14, decoder_1_out15, decoder_1_out16, decoder_1_out17, decoder_1_out18,
       decoder_1_out19, decoder_1_out20, decoder_1_out21, decoder_1_out22, decoder_1_out23, decoder_1_out24,
       decoder_1_out25, decoder_1_out26, decoder_1_out27, decoder_1_out28, decoder_1_out29, decoder_1_out30,
       decoder_1_out31;
  wire [31:0] _0_q, _1_q, _2_q, _3_q, _4_q, _5_q, _6_q, _7_q, _8_q, _9_q, register_1_q, register_2_q,
       register_3_q, register_4_q, register_5_q, register_6_q, register_7_q, register_8_q, register_9_q,
       register_10_q, register_11_q, register_12_q, register_13_q, register_14_q, register_15_q,
       register_16_q, register_17_q, register_18_q, register_19_q, register_20_q, register_21_q,
       register_22_q;

  Decoder #(.select(5), .enable("false")) decoder_1 (
    .out0(decoder_1_out0), .out1(decoder_1_out1), .out2(decoder_1_out2), .out3(decoder_1_out3),
    .out4(decoder_1_out4), .out5(decoder_1_out5), .out6(decoder_1_out6), .out7(decoder_1_out7),
    .out8(decoder_1_out8), .out9(decoder_1_out9), .out10(decoder_1_out10), .out11(decoder_1_out11),
    .out12(decoder_1_out12), .out13(decoder_1_out13), .out14(decoder_1_out14), .out15(decoder_1_out15),
    .out16(decoder_1_out16), .out17(decoder_1_out17), .out18(decoder_1_out18), .out19(decoder_1_out19),
    .out20(decoder_1_out20), .out21(decoder_1_out21), .out22(decoder_1_out22), .out23(decoder_1_out23),
    .out24(decoder_1_out24), .out25(decoder_1_out25), .out26(decoder_1_out26), .out27(decoder_1_out27),
    .out28(decoder_1_out28), .out29(decoder_1_out29), .out30(decoder_1_out30), .out31(decoder_1_out31),
    .sel(Write_Reg_num));
  and and_1 (and_1_out, Write_Enable, decoder_1_out0);
  and and_2 (and_2_out, Write_Enable, decoder_1_out1);
  and and_3 (and_3_out, Write_Enable, decoder_1_out2);
  and and_4 (and_4_out, Write_Enable, decoder_1_out3);
  and and_5 (and_5_out, Write_Enable, decoder_1_out4);
  and and_6 (and_6_out, Write_Enable, decoder_1_out5);
  and and_7 (and_7_out, Write_Enable, decoder_1_out6);
  and and_8 (and_8_out, Write_Enable, decoder_1_out7);
  and and_9 (and_9_out, Write_Enable, decoder_1_out8);
  and and_10 (and_10_out, Write_Enable, decoder_1_out9);
  and and_11 (and_11_out, Write_Enable, decoder_1_out10);
  and and_12 (and_12_out, Write_Enable, decoder_1_out11);
  and and_13 (and_13_out, Write_Enable, decoder_1_out12);
  and and_14 (and_14_out, Write_Enable, decoder_1_out13);
  and and_15 (and_15_out, Write_Enable, decoder_1_out14);
  and and_16 (and_16_out, Write_Enable, decoder_1_out15);
  and and_17 (and_17_out, Write_Enable, decoder_1_out16);
  and and_18 (and_18_out, Write_Enable, decoder_1_out17);
  and and_19 (and_19_out, Write_Enable, decoder_1_out18);
  and and_20 (and_20_out, Write_Enable, decoder_1_out19);
  and and_21 (and_21_out, Write_Enable, decoder_1_out20);
  and and_22 (and_22_out, Write_Enable, decoder_1_out21);
  and and_23 (and_23_out, Write_Enable, decoder_1_out22);
  and and_24 (and_24_out, Write_Enable, decoder_1_out23);
  and and_25 (and_25_out, Write_Enable, decoder_1_out24);
  and and_26 (and_26_out, Write_Enable, decoder_1_out25);
  and and_27 (and_27_out, Write_Enable, decoder_1_out26);
  and and_28 (and_28_out, Write_Enable, decoder_1_out27);
  and and_29 (and_29_out, Write_Enable, decoder_1_out28);
  and and_30 (and_30_out, Write_Enable, decoder_1_out29);
  and and_31 (and_31_out, Write_Enable, decoder_1_out30);
  and and_32 (and_32_out, Write_Enable, decoder_1_out31);
  Register #(.width(32), .Select("high")) _0 (.D({32{1'b0}}), .en(and_1_out), .Q(_0_q), .clk(Clock));  // open: clr
  Register #(.width(32), .Select("high")) _1 (.D(Din), .en(and_2_out), .Q(_1_q), .clk(Clock));  // open: clr
  Register #(.width(32), .Select("high")) _2 (.D(Din), .en(and_3_out), .Q(_2_q), .clk(Clock));  // open: clr
  Register #(.width(32), .Select("high")) _3 (.D(Din), .en(and_4_out), .Q(_3_q), .clk(Clock));  // open: clr
  Register #(.width(32), .Select("high")) _4 (.D(Din), .en(and_5_out), .Q(_4_q), .clk(Clock));  // open: clr
  Register #(.width(32), .Select("high")) _5 (.D(Din), .en(and_6_out), .Q(_5_q), .clk(Clock));  // open: clr
  Register #(.width(32), .Select("high")) _6 (.D(Din), .en(and_7_out), .Q(_6_q), .clk(Clock));  // open: clr
  Register #(.width(32), .Select("high")) _7 (.D(Din), .en(and_8_out), .Q(_7_q), .clk(Clock));  // open: clr
  Register #(.width(32), .Select("high")) _8 (.D(Din), .en(and_9_out), .Q(_8_q), .clk(Clock));  // open: clr
  Register #(.width(32), .Select("high")) _9 (.D(Din), .en(and_10_out), .Q(_9_q), .clk(Clock));  // open: clr
  Register #(.width(32), .Select("high")) register_1 (
    .D(Din), .en(and_11_out), .Q(register_1_q), .clk(Clock));  // open: clr
  Register #(.width(32), .Select("high")) register_2 (
    .D(Din), .en(and_12_out), .Q(register_2_q), .clk(Clock));  // open: clr
  Register #(.width(32), .Select("high")) register_3 (
    .D(Din), .en(and_13_out), .Q(register_3_q), .clk(Clock));  // open: clr
  Register #(.width(32), .Select("high")) register_4 (
    .D(Din), .en(and_14_out), .Q(register_4_q), .clk(Clock));  // open: clr
  Register #(.width(32), .Select("high")) register_5 (
    .D(Din), .en(and_15_out), .Q(register_5_q), .clk(Clock));  // open: clr
  Register #(.width(32), .Select("high")) register_6 (
    .D(Din), .en(and_16_out), .Q(register_6_q), .clk(Clock));  // open: clr
  Register #(.width(32), .Select("high")) register_7 (
    .D(Din), .en(and_17_out), .Q(register_7_q), .clk(Clock));  // open: clr
  Register #(.width(32), .Select("high")) register_8 (
    .D(Din), .en(and_18_out), .Q(register_8_q), .clk(Clock));  // open: clr
  Register #(.width(32), .Select("high")) register_9 (
    .D(Din), .en(and_19_out), .Q(register_9_q), .clk(Clock));  // open: clr
  Register #(.width(32), .Select("high")) register_10 (
    .D(Din), .en(and_20_out), .Q(register_10_q), .clk(Clock));  // open: clr
  Register #(.width(32), .Select("high")) register_11 (
    .D(Din), .en(and_21_out), .Q(register_11_q), .clk(Clock));  // open: clr
  Register #(.width(32), .Select("high")) register_12 (
    .D(Din), .en(and_22_out), .Q(register_12_q), .clk(Clock));  // open: clr
  Register #(.width(32), .Select("high")) register_13 (
    .D(Din), .en(and_23_out), .Q(register_13_q), .clk(Clock));  // open: clr
  Register #(.width(32), .Select("high")) register_14 (
    .D(Din), .en(and_24_out), .Q(register_14_q), .clk(Clock));  // open: clr
  Register #(.width(32), .Select("high")) register_15 (
    .D(Din), .en(and_25_out), .Q(register_15_q), .clk(Clock));  // open: clr
  Register #(.width(32), .Select("high")) register_16 (
    .D(Din), .en(and_26_out), .Q(register_16_q), .clk(Clock));  // open: clr
  Register #(.width(32), .Select("high")) register_17 (
    .D(Din), .en(and_27_out), .Q(register_17_q), .clk(Clock));  // open: clr
  Register #(.width(32), .Select("high")) register_18 (
    .D(Din), .en(and_28_out), .Q(register_18_q), .clk(Clock));  // open: clr
  Register #(.width(32), .Select("high")) register_19 (
    .D(Din), .en(and_29_out), .Q(register_19_q), .clk(Clock));  // open: clr
  Register #(.width(32), .Select("high")) register_20 (
    .D(Din), .en(and_30_out), .Q(register_20_q), .clk(Clock));  // open: clr
  Register #(.width(32), .Select("high")) register_21 (
    .D(Din), .en(and_31_out), .Q(register_21_q), .clk(Clock));  // open: clr
  Register #(.width(32), .Select("high")) register_22 (
    .D(Din), .en(and_32_out), .Q(register_22_q), .clk(Clock));  // open: clr
  Multiplexer #(.select(5), .width(32), .enable("false")) multiplexer_1 (
    .in0(_0_q), .in1(_1_q), .in2(_2_q), .in3(_3_q), .in4(_4_q), .in5(_5_q), .in6(_6_q), .in7(_7_q),
    .in8(_8_q), .in9(_9_q), .in10(register_1_q), .in11(register_2_q), .in12(register_3_q),
    .in13(register_4_q), .in14(register_5_q), .in15(register_6_q), .in16(register_7_q), .in17(register_8_q),
    .in18(register_9_q), .in19(register_10_q), .in20(register_11_q), .in21(register_12_q),
    .in22(register_13_q), .in23(register_14_q), .in24(register_15_q), .in25(register_16_q),
    .in26(register_17_q), .in27(register_18_q), .in28(register_19_q), .in29(register_20_q),
    .in30(register_21_q), .in31(register_22_q), .out(Reg1Out), .sel(R1_num));
  Multiplexer #(.select(5), .width(32), .enable("false")) multiplexer_2 (
    .in0(_0_q), .in1(_1_q), .in2(_2_q), .in3(_3_q), .in4(_4_q), .in5(_5_q), .in6(_6_q), .in7(_7_q),
    .in8(_8_q), .in9(_9_q), .in10(register_1_q), .in11(register_2_q), .in12(register_3_q),
    .in13(register_4_q), .in14(register_5_q), .in15(register_6_q), .in16(register_7_q), .in17(register_8_q),
    .in18(register_9_q), .in19(register_10_q), .in20(register_11_q), .in21(register_12_q),
    .in22(register_13_q), .in23(register_14_q), .in24(register_15_q), .in25(register_16_q),
    .in26(register_17_q), .in27(register_18_q), .in28(register_19_q), .in29(register_20_q),
    .in30(register_21_q), .in31(register_22_q), .out(Reg2Out), .sel(R2_num));

  // Other names for the same wires on the sheet: CLK = Clock; RA[4:0] = R1_num; RB[4:0] = R2_num; RDA[31:0] = Reg1Out;
  //   RDB[31:0] = Reg2Out; RW[4:0] = Write_Reg_num; WE = Write_Enable

  // Notes on the sheet:
  //   输入引脚
  //   请勿修改引脚名称、电路名称及电路封装外观
  //   提示：使用译码器、多路选择器和32位寄存器及逻辑门实现寄存器堆，禁止直接使用存储器组件。
  //   输出引脚
endmodule

module \立即数扩展器  (
  input  [31:0] Instr,
  input  [2:0] Extop,
  output [31:0] imm
);

  wire [11:0] bit_extender_4_out;
  wire [19:0] bit_extender_3_out;
  wire [26:0] bit_extender_2_out;
  wire [31:0] bit_extender_1_out;

  assign bit_extender_1_out = {{20{Instr[31]}}, Instr[31:20]};  // Bit_Extender bit_extender_1
  assign bit_extender_2_out = {{20{Instr[31]}}, Instr[31:25]};  // Bit_Extender bit_extender_2
  assign bit_extender_3_out = {{19{Instr[31]}}, Instr[31]};  // Bit_Extender bit_extender_3
  assign bit_extender_4_out = {{11{Instr[31]}}, Instr[31]};  // Bit_Extender bit_extender_4
  Multiplexer #(.select(3), .width(32), .enable("false")) multiplexer_1 (
    .in0(bit_extender_1_out), .in1({Instr[31:12], {12{1'b0}}}), .in2({bit_extender_2_out, Instr[11:7]}),
    .in3({bit_extender_3_out, Instr[7], Instr[30:25], Instr[11:8], 1'b0}),
    .in4({bit_extender_4_out, Instr[19:12], Instr[20], Instr[30:21], 1'b0}), .out(imm), .sel(Extop));  // open: in5, in6, in7

  // Notes on the sheet:
  //   Extop: pull=down
  //   Instr: pull=down
  //   输入引脚
  //   输出引脚
endmodule

module DataRAM (
  input  CLK,
  input  CLR,
  input  WE,
  input  [2:0] MemOp,
  input  [17:0] Addr,
  input  [31:0] Din,
  output AlignErr,
  output [31:0] DataOut
);

  wire and_3_out, and_4_out, and_5_out, and_6_out, and_7_out, and_8_out, and_9_out, and_10_out, and_11_out,
       and_12_out, and_13_out, or_1_out, or_2_out, or_3_out, or_4_out, or_5_out, or_6_out, or_7_out;
  wire [1:0] and_2_out;
  wire [7:0] multiplexer_1_out, multiplexer_2_out, multiplexer_3_out, multiplexer_5_out, ram_3_data,
       ram_4_data;
  wire [15:0] multiplexer_4_out, ram_1_data;
  wire [31:0] bit_extender_1_out, bit_extender_2_out, bit_extender_3_out, bit_extender_4_out;

  and and_1 (and_2_out[1], ~MemOp[0], ~MemOp[1], ~MemOp[2]);  // AND_Gate
  and and_2 (and_2_out[0], ~MemOp[0], MemOp[1], MemOp[2]);  // AND_Gate
  and and_3 (and_3_out, MemOp[0], ~MemOp[1], MemOp[2]);  // AND_Gate
  Multiplexer #(.width(8), .enable("false")) multiplexer_1 (
    .in0(Din[7:0]), .in1(Din[15:8]), .out(multiplexer_1_out), .sel(or_2_out));
  RAM #(.addrWidth(18), .bus("separate"), .Select("high")) ram_1 (
    .addr({Addr[17:2], 2'b00}), .din(Din[7:0]), .data(ram_1_data[7:0]), .str(and_13_out), .sel(or_4_out),
    .clk(CLK), .ld(or_4_out), .clr(CLR));
  RAM #(.addrWidth(18), .bus("separate"), .Select("high")) ram_2 (
    .addr({Addr[17:2], 2'b00}), .din(multiplexer_1_out), .data(ram_1_data[15:8]), .str(and_13_out),
    .sel(or_5_out), .clk(CLK), .ld(or_5_out), .clr(CLR));
  or or_1 (or_1_out, and_2_out[1], and_2_out[0], and_3_out);
  Multiplexer #(.width(8), .enable("false")) multiplexer_2 (
    .in0(Din[7:0]), .in1(Din[23:16]), .out(multiplexer_2_out), .sel(and_2_out[1]));
  and and_4 (and_4_out, ~Addr[0], ~MemOp[0], MemOp[1]);  // AND_Gate
  and and_5 (and_5_out, MemOp[0], ~MemOp[1]);  // AND_Gate
  or or_2 (or_2_out, and_2_out[1], and_2_out[0]);
  and and_6 (and_6_out, ~Addr[0], ~Addr[1], ~MemOp[2], ~MemOp[0], ~MemOp[1]);  // AND_Gate
  and and_7 (and_7_out, ~Addr[0], ~Addr[1], MemOp[0], ~MemOp[1]);  // AND_Gate
  and and_8 (and_8_out, Addr[0], ~Addr[1], MemOp[0], ~MemOp[1]);  // AND_Gate
  and and_9 (and_9_out, ~Addr[0], Addr[1], MemOp[0], ~MemOp[1]);  // AND_Gate
  and and_10 (and_10_out, Addr[0], Addr[1], MemOp[0], ~MemOp[1]);  // AND_Gate
  and and_11 (and_11_out, ~Addr[0], ~Addr[1], ~MemOp[0], MemOp[1]);  // AND_Gate
  and and_12 (and_12_out, ~Addr[0], Addr[1], ~MemOp[0], MemOp[1]);  // AND_Gate
  RAM #(.addrWidth(18), .bus("separate"), .Select("high")) ram_3 (
    .addr({Addr[17:2], 2'b00}), .din(multiplexer_2_out), .data(ram_3_data), .str(and_13_out), .sel(or_6_out),
    .clk(CLK), .ld(or_6_out), .clr(CLR));
  Multiplexer #(.select(2), .width(8), .enable("false")) multiplexer_3 (
    .in0(Din[7:0]), .in1(Din[15:8]), .in2(Din[31:24]), .out(multiplexer_3_out), .sel(and_2_out));  // open: in3
  or or_3 (or_3_out, and_4_out, and_5_out, and_6_out);
  not not_1 (AlignErr, or_3_out);
  or or_4 (or_4_out, and_6_out, and_7_out, and_11_out);
  or or_5 (or_5_out, and_6_out, and_8_out, and_11_out);
  or or_6 (or_6_out, and_6_out, and_9_out, and_12_out);
  or or_7 (or_7_out, and_6_out, and_10_out, and_12_out);
  and and_13 (and_13_out, or_1_out, WE);
  RAM #(.addrWidth(18), .bus("separate"), .Select("high")) ram_4 (
    .addr({Addr[17:2], 2'b00}), .din(multiplexer_3_out), .data(ram_4_data), .str(and_13_out), .sel(or_7_out),
    .clk(CLK), .ld(or_7_out), .clr(CLR));
  Multiplexer #(.width(16), .enable("false")) multiplexer_4 (
    .in0(ram_1_data), .in1({ram_4_data, ram_3_data}), .out(multiplexer_4_out), .sel(Addr[1]));
  Multiplexer #(.select(2), .width(8), .enable("false")) multiplexer_5 (
    .in0(ram_1_data[7:0]), .in1(ram_1_data[15:8]), .in2(ram_3_data), .in3(ram_4_data),
    .out(multiplexer_5_out), .sel(Addr[1:0]));
  assign bit_extender_1_out = {{16{1'b0}}, multiplexer_4_out};  // Bit_Extender bit_extender_1
  assign bit_extender_2_out = {{16{multiplexer_4_out[15]}}, multiplexer_4_out};  // Bit_Extender bit_extender_2
  assign bit_extender_3_out = {{24{1'b0}}, multiplexer_5_out};  // Bit_Extender bit_extender_3
  assign bit_extender_4_out = {{24{multiplexer_5_out[7]}}, multiplexer_5_out};  // Bit_Extender bit_extender_4
  Multiplexer #(.select(3), .width(32), .enable("false")) multiplexer_6 (
    .in0({ram_4_data, ram_3_data, ram_1_data}), .in1(bit_extender_3_out), .in2(bit_extender_1_out),
    .in5(bit_extender_4_out), .in6(bit_extender_2_out), .out(DataOut), .sel(MemOp));  // open: in3, in4, in7

  // Other names for the same wires on the sheet: Dout[31:0] = DataOut

  // Notes on the sheet:
  //   输入引脚
  //   请勿修改引脚名称、电路名称及电路封装外观
  //   为了后续实验中的引用，不要修改MemOp的编码定义、引脚名称和在布局中的位置。
  //   32位数据存储器，按字节分4片存储，可按照字节、半字和字进行存储；读取字节或半字时，支持0扩展和符号位扩展。
  //   输出引脚
endmodule

module ALU (
  input  [3:0] ALUctr,
  input  [31:0] A,
  input  [31:0] B,
  output Zero,
  output [31:0] S
);

  // Probe on A
  // Probe on B
  // Probe on S

  // Other names for the same wires on the sheet: Result[31:0] = S

  // Notes on the sheet:
  //   A: pull=down
  //   B: pull=down
  //   ALUctr: pull=down
  //   输入引脚
  //   请勿修改引脚名称、电路名称及电路封装外观
  //   提示：使用32位并行加法器子电路、桶形移位器、ALU控制子电路实现32位ALU
  //   功能说明:32位ALU，输入32位操作数A、B，4位控制信号ALUctr，输出32位结果Reseult和1位Zero标志位
  //   输出引脚
  //   操作数和结果
endmodule

module ALUctrl (
  input  [3:0] ALUctr,
  output SUBctr,
  output SFTctr,
  output SIGctr,
  output ALctr,
  output [2:0] OPctr
);


  // Other names for the same wires on the sheet: LRctr = SFTctr

  // Notes on the sheet:
  //   输入引脚
  //   ALU操作控制信号生成部件
  //   输出引脚
endmodule

module Adder32 (
  input  Cin,
  input  [31:0] X,
  input  [31:0] Y,
  output CF,
  output Cout,
  output OF,
  output SF,
  output [31:0] S,
  output ZF
);

  // Probe on X
  // Probe on Y
  // Probe on S

  // Notes on the sheet:
  //   X: pull=down
  //   Cin: pull=down
  //   Y: pull=down
  //   输入引脚区
  //   输出引脚区
  //   请勿修改引脚名称、电路名称及电路封装外观
  //   提示：使用16位并行加法器子电路实现32位快速加法器
  //   功能说明:32位Adder  S=X+Y，Cout为最高位进位位，Cin为进位输入， S为和，溢出OF、进位CF、零ZF、符号SF。
  //   +
  //   =
  //   无符号加法
endmodule

// 移位器
module Shifter32 (
  input  [4:0] shamt,
  input  L_R,
  input  A_L,
  input  [31:0] DataIn,
  output [31:0] DataOut
);


  // Other names for the same wires on the sheet: Arth_Logic = A_L; Din[31:0] = DataIn; Dout[31:0] = DataOut;
  //   Left_Right = L_R

  // Notes on the sheet:
  //   L/R,A/L: 00逻辑右移，01算术右移，10逻辑左移，11：循环左移
  //   输入引脚
  //   请勿修改引脚名称、电路名称及电路封装外观
  //   提示：使用多路选择器、逻辑门实现32位桶形移位器，禁止直接使用移位器组件。
  //   输出引脚
endmodule

module Adder16 (
  input  C0,
  input  [15:0] X,
  input  [15:0] Y,
  output C16,
  output Pg,
  output Gg,
  output [15:0] S
);

  // Probe on X
  // Probe on Y
  // Probe on S

  // Notes on the sheet:
  //   X: pull=down
  //   Y: pull=down
  //   C0: pull=down
  //   输入引脚区
  //   请勿修改引脚名称、电路名称及电路封装外观
  //   提示：使用4位先行进位加法器和CLU子电路实现16位并行加法器
  //   功能说明:16位Adder  S=X+Y，C16为最高位进位位，C0为进位输入， Pg、Gg为成组进位生成传递函数
  //   输出引脚区
  //   +
  //   =
  //   无符号加法
endmodule

module CLA4 (
  input  [3:0] X,
  input  [3:0] Y,
  input  Cin,
  output [3:0] F,
  output Cout,
  output Pg,
  output Gg
);

  Hex_Digit_Display hex_digit_display_1 (.value(X));  // open: dp
  Hex_Digit_Display hex_digit_display_2 (.value(Y));  // open: dp
  Hex_Digit_Display hex_digit_display_3 (.value(F));  // open: dp

  // Other names for the same wires on the sheet: Z[3:0] = F

  // Notes on the sheet:
  //   +
  //   =
  //   输出
  //   输入
  //   请勿修改引脚名称、电路名称及电路封装外观
  //   提示：使用全加器和CLU子电路实现四位先行进位加法器CLA4
endmodule

module CLU4 (
  input  P0,
  input  P1,
  input  P2,
  input  P3,
  input  G0,
  input  G1,
  input  G2,
  input  G3,
  input  C0,
  output C1,
  output C3,
  output C2,
  output C4,
  output Pg,
  output Gg
);


  // Notes on the sheet:
  //   输入引脚
  //   请勿修改引脚名称、电路名称及电路封装外观
  //   提示：使用逻辑门电路实现4位四位先行进位部件CLU，Pg、Gg为成组进位生成传递函数
  //   输出引脚
endmodule

module FA (
  input  A,
  input  B,
  input  Cin,
  output F,
  output P,
  output G
);


  // Notes on the sheet:
  //   输入引脚
  //   请勿修改引脚名称、电路名称及电路封装外观
  //   输出引脚
endmodule
