// Logisim project lab6.1.circ as structural Verilog: 1 circuit, main circuit 控制器
module \控制器  (
  input  [6:0] opcode,
  input  [2:0] funct3,
  input  [6:0] funct7,
  output [2:0] ExtOp,
  output RegWr,
  output [2:0] BandJ,
  output ALUASrc,
  output [1:0] ALUBSrc,
  output [3:0] ALUctr,
  output MemtoReg,
  output [2:0] MemOp,
  output MemWr
);

  wire and_1_out, and_2_out, and_3_out, and_4_out, and_5_out, and_6_out, and_7_out, and_8_out, and_9_out,
       and_10_out, comparator_1_eq, comparator_2_eq, comparator_4_eq, comparator_5_eq, comparator_6_eq,
       comparator_10_eq, not_1_out, or_1_out, or_5_out, or_6_out, or_7_out, or_8_out, or_9_out;

  Comparator #(.width(7)) comparator_1 (.a(opcode), .b(7'b0110111), .eq(comparator_1_eq));  // open: gt, lt
  Comparator #(.width(7)) comparator_2 (.a(opcode), .b(7'b0010111), .eq(comparator_2_eq));  // open: gt, lt
  Comparator #(.width(7)) comparator_3 (.a(opcode), .b(7'b1101111), .eq(ExtOp[2]));  // open: gt, lt
  Comparator #(.width(7)) comparator_4 (.a(opcode), .b(7'b1100111), .eq(comparator_4_eq));  // open: gt, lt
  Comparator #(.width(7)) comparator_5 (.a(opcode), .b(7'b0010011), .eq(comparator_5_eq));  // open: gt, lt
  Comparator #(.width(7)) comparator_6 (.a(opcode), .b(7'b0110011), .eq(comparator_6_eq));  // open: gt, lt
  Comparator #(.width(7)) comparator_7 (.a(opcode), .b(7'b1100011), .eq(BandJ[2]));  // open: gt, lt
  Comparator #(.width(7)) comparator_8 (.a(opcode), .b(7'b0000011), .eq(MemtoReg));  // open: gt, lt
  Comparator #(.width(7)) comparator_9 (.a(opcode), .b(7'b0100011), .eq(MemWr));  // open: gt, lt
  and and_1 (and_1_out, comparator_5_eq, funct3[0], ~funct3[1], funct3[2]);  // AND_Gate
  Comparator #(.width(7)) comparator_10 (.a({7{1'b0}}), .b(opcode), .eq(comparator_10_eq));  // open: gt, lt
  not not_1 (not_1_out, or_1_out);
  or or_1 (or_1_out, BandJ[2], MemWr);
  or or_2 (ALUASrc, comparator_2_eq, ExtOp[2], comparator_4_eq);
  or or_3 (ALUBSrc[0], ExtOp[2], comparator_4_eq);
  or or_4 (ALUBSrc[1], comparator_1_eq, comparator_2_eq, comparator_5_eq, MemtoReg, MemWr);
  and and_2 (and_2_out, BandJ[2], funct3[0]);
  and and_3 (and_3_out, BandJ[2], funct3[2]);
  and and_4 (and_4_out, comparator_5_eq, funct3[0]);
  and and_5 (and_5_out, comparator_6_eq, funct3[0]);
  and and_6 (and_6_out, BandJ[2], funct3[1]);
  and and_7 (and_7_out, comparator_5_eq, funct3[1]);
  and and_8 (and_8_out, comparator_6_eq, funct3[1]);
  and and_9 (and_9_out, funct3[2], or_5_out);
  or or_5 (or_5_out, comparator_5_eq, comparator_6_eq);
  and and_10 (and_10_out, funct7[5], or_6_out);
  or or_6 (or_6_out, and_1_out, comparator_6_eq);
  or or_7 (or_7_out, MemtoReg, MemWr);
  or or_8 (or_8_out, MemtoReg, MemWr);
  or or_9 (or_9_out, MemtoReg, MemWr);
  and and_11 (RegWr, ~comparator_10_eq, not_1_out);  // AND_Gate
  or or_10 (ExtOp[0], comparator_1_eq, comparator_2_eq, BandJ[2]);
  or or_11 (ExtOp[1], BandJ[2], MemWr);
  or or_12 (BandJ[0], ExtOp[2], and_2_out);
  or or_13 (BandJ[1], comparator_4_eq, and_3_out);
  or or_14 (ALUctr[0], comparator_1_eq, and_4_out, and_5_out, and_6_out);
  or or_15 (ALUctr[1], comparator_1_eq, and_7_out, and_8_out, BandJ[2]);
  or or_16 (ALUctr[2], comparator_1_eq, and_9_out);
  or or_17 (ALUctr[3], comparator_1_eq, and_10_out);
  and and_12 (MemOp[0], ~funct3[0], ~funct3[1], or_7_out);  // AND_Gate
  and and_13 (MemOp[1], funct3[0], or_8_out);
  and and_14 (MemOp[2], ~funct3[1], ~funct3[2], or_9_out);  // AND_Gate

  // Notes on the sheet:
  //   输入引脚
  //   U-lui
  //   U-auipc
  //   J-jal
  //   J-jalr
  //   I-Arith
  //   R-Arith
  //   B-Instr
  //   I-load
  //   S-Instr
  //   请勿修改引脚名称、电路名称及电路封装外观
  //   提示：根据指令种类，把7位指令code用一位指令类型标志位来表示，再通过功能码来区分具体指令，生成控制信号。
  //   输出引脚
endmodule
