// Logisim project lab6.2.circ as structural Verilog: 16 circuits, main circuit main
module main (
  input  ReSet,
  input  [31:0] Init_Addr,
  input  clk,
  output [31:0] PC,
  output [31:0] IR,
  output [31:0] BusW,
  output [31:0] Din,
  output [15:0] Cycles,
  output Halt
);

  wire alu_1_zero, ALUASrc, clk_out, clk_t, MemtoReg, MemWr, not_2_out, NPCASrc, NPCBSrc, RegWr;
  wire [1:0] ALUBSrc;
  wire [2:0] BandJ, ExtOp, idu_1_funct3, MemOp;
  wire [3:0] ALUctr;
  wire [6:0] idu_1_funct7, idu_1_opcode;
  wire [13:0] alu_1_s_2;
  wire [17:0] alu_1_s;
  wire [31:0] dataram_1_dataout, idu_1_busa, idu_1_dataa, idu_1_datab, idu_1_imm;

  Clock u_clk (.out(clk_out));
  not not_1 (clk_t, clk_out);
  IFU ifu_1 (
    .CLK(clk_t), .Reset(ReSet), .NPCASrc(NPCASrc), .NPCBSrc(NPCBSrc), .Initial_Address(Init_Addr),
    .Imm(idu_1_imm), .BusA(idu_1_busa), .PC(PC), .halt(Halt));
  \控制器  \u_控制器_1  (
    .opcode(idu_1_opcode), .ExtOp(ExtOp), .RegWr(RegWr), .BandJ(BandJ), .funct3(idu_1_funct3),
    .ALUASrc(ALUASrc), .ALUBSrc(ALUBSrc), .ALUctr(ALUctr), .funct7(idu_1_funct7), .MemtoReg(MemtoReg),
    .MemOp(MemOp), .MemWr(MemWr), .Halt(Halt));
  ROM #(.addrWidth(16), .dataWidth(32), .Select("high")) rom_1 (.addr(PC[17:2]), .data(IR), .sel(1'b1));
  IDU idu_1 (
    .OpCode(idu_1_opcode), .ExtOp(ExtOp), .RegWr(RegWr), .Imm(idu_1_imm), .Funct3(idu_1_funct3),
    .ALUASrc(ALUASrc), .ALUBSrc(ALUBSrc), .Funct7(idu_1_funct7), .CLK(clk_t), .IR(IR), .BusW(BusW), .PC(PC),
    .DataA(idu_1_dataa), .DataB(idu_1_datab), .BusA(idu_1_busa), .BusB(Din));
  // Probe on Cycles
  Counter #(.width(16), .max('hffff), .behavior("old")) \u_计数器  (
    .count(not_2_out), .Q(Cycles), .clk(clk_t), .clr(ReSet));  // open: load, D, carry, preset
  not not_2 (not_2_out, Halt);
  ALU alu_1 (.A(idu_1_dataa), .B(idu_1_datab), .ALUctr(ALUctr), .S({alu_1_s_2, alu_1_s}), .Zero(alu_1_zero));
  BandJ bandj_1 (.BandJ(BandJ), .NPCASrc(NPCASrc), .Zero(alu_1_zero), .NPCBSrc(NPCBSrc), .Result0(alu_1_s[0]));
  DataRAM dataram_1 (
    .Addr(alu_1_s), .Din(Din), .CLK(clk_t), .CLR(ReSet), .WE(MemWr), .MemOp(MemOp),
    .DataOut(dataram_1_dataout));  // open: AlignErr
  Multiplexer #(.width(32), .enable("false")) multiplexer_1 (
    .in0({alu_1_s_2, alu_1_s}), .in1(dataram_1_dataout), .out(BusW), .sel(MemtoReg));

  // Notes on the sheet:
  //   输入引脚
  //   请勿修改引脚名称、电路名称及电路封装外观
  //   指令存储器和数据存储器数据位都是32位，指令存储器编址以字为单位，数据存储器编址以字节为单位。
  //   引用取指令部件、取操作数部件、ALU部件、数据存储器、分支控制器、指令存储器等部件，完成单周期CPU设计。
  //   contents of rom_1 (hex, n*v repeats v):
  //   80000037 7ff00013 10c0b3 100193 14101863 800000b7 ffff8137 208733 7fff83b7 200193 12771c63 ff010b7
  //   ff008093 f0f0f137 f010113 20f7b3 f003b7 f038393 300193 10779a63 100093 3f00113 209833 800003b7
  //   400193 e781e63 800000b7 e00113 4020d8b3 fffe03b7 500193 e789263 800000b7 7ff0a913 100393 600193
  //   c791863 800000b7 7ff0b993 393 700193 a799e63 97 cc08093 ee00113 208023 ff00113 2080a3 c000113 208123
  //   113 2081a3 108a03 fff00393 800193 87a1263 da83 103b7 fee38393 900193 67a9863 1509223 209b03 c000393
  //   a00193 47b1e63 1609323 ab83 c103b7 fee38393 b00193 47b9263 40ac03 c103b7 fee38393 c00193 27c1863 c97
  //   10c8ce7 33 200006f 397 ff838393 d00193 7c9863 c10537 fee50513
  //   输出引脚
  //   状态元件的触发条件都设置成上升沿触发，时钟输入信号通过反相器输入。
  //   程序执行周期数
endmodule

module BandJ (
  input  [2:0] BandJ,
  input  Zero,
  input  Result0,
  output NPCASrc,
  output NPCBSrc
);

  wire not_1_out, or_1_out;

  not not_1 (not_1_out, Zero);
  or or_1 (or_1_out, Zero, ~Result0);  // OR_Gate
  Multiplexer #(.select(3), .enable("false")) multiplexer_1 (
    .in0(1'b0), .in1(1'b1), .in2(1'b1), .in4(Zero), .in5(not_1_out), .in6(Result0), .in7(or_1_out),
    .out(NPCBSrc), .sel(BandJ));  // open: in3
  and and_1 (NPCASrc, ~BandJ[0], BandJ[1], ~BandJ[2]);  // AND_Gate

  // Notes on the sheet:
  //   BandJ: pull=down
  //   Zero: pull=down
  //   输入信号
  //   请勿修改引脚名称、电路名称及电路封装外观
  //   不要修改控制信号的编码定义、引脚名称和在布局中的位置。
  //   输出信号
endmodule

module IFU (
  input  [31:0] Initial_Address,
  input  [31:0] Imm,
  input  [31:0] BusA,
  input  CLK,
  input  Reset,
  input  halt,
  input  NPCASrc,
  input  NPCBSrc,
  output [31:0] PC
);

  wire not_1_out, not_2_out;
  wire [31:0] adder_1_out, IR, multiplexer_1_out, multiplexer_2_out, multiplexer_3_out;

  Multiplexer #(.width(32), .enable("false")) multiplexer_1 (
    .in0(PC), .in1(BusA), .out(multiplexer_1_out), .sel(NPCASrc));
  Multiplexer #(.width(32), .enable("false")) multiplexer_2 (
    .in0(32'h4), .in1(Imm), .out(multiplexer_2_out), .sel(NPCBSrc));
  Adder #(.width(32)) adder_1 (.a(multiplexer_1_out), .b(multiplexer_2_out), .out(adder_1_out));  // open: cin, cout
  Multiplexer #(.width(32), .enable("false")) multiplexer_3 (
    .in0(Initial_Address), .in1(adder_1_out), .out(multiplexer_3_out), .sel(not_1_out));
  not not_1 (not_1_out, Reset);
  Register #(.width(32), .Select("high")) register_1 (
    .D(multiplexer_3_out), .en(not_2_out), .Q(PC), .clk(CLK), .clr(Reset));
  not not_2 (not_2_out, halt);
  ROM #(.addrWidth(16), .dataWidth(32), .Select("high")) rom_1 (.addr(PC[17:2]), .data(IR));

  // Other names for the same wires on the sheet: Init_Addr[31:0] = Initial_Address

  // Notes on the sheet:
  //   NPCBSrc: pull=down
  //   NPCASrc: pull=down
  //   BusA: pull=down
  //   Imm: pull=down
  //   请勿修改引脚名称、电路名称及电路封装外观
  //   指令存储器256KB，数据位为32位，地址位为16位。PC寄存器数据宽度32位，片选信号高电平有效
  //   输入信号
  //   输出信号
  //   contents of rom_1 (hex, n*v repeats v):
  //   256*0 2083 8133 106213 406293 fff06313 4410663 106193 406393 806413 21b5b3 2058063 3a483 42503
  //   a4b5b3 458c63 a3a023 942023 c0006f 610133 fc9ff06f 4181b3 5383b3 540433 fc9ff06f 6f 0 0 413 9117
  //   ffc10113 94000ef 50463 8067 ff010113 100513 112623 74000ef ff010113 812423 912223 15c00413 1212023
  //   112623 c400493 9840913 442783 42703 4a503 440413 e787b3 40f50533 153513 f42223 448493 fa5ff0ef
  //   fd241ce3 100513 f99ff0ef c12083 812403 412483 12903 513 1010113 8067 1ea02e23 6f ff010113 b800513
  //   112623 f7dff0ef 1ea02e23 6f 0 1 1 2 3 5 8 d 15 22 37 59 90 e9 179 262 3db 63d a18 1055 1a6d 2ac2
  //   452f 6ff1 b520 12511 1da31 2ff42 4d973 7d8b5 cb228 148add 213d05 35c7e2 5704e7 8cccc9 e3d1b0 1709e79
  //   2547029 3c50ea2 6197ecb 1 1 deadbeef 395*0 413 9117 ffc10113 ec000ef 50463 8067 ff010113 100513
  //   112623 cc000ef ff010113 19400813 112623 812423 912223 1212023 100793 f82223 f82023 880593 7c80313
  //   100713 19800513 100893 50493 50793 100693 80006f 7a703 d70633 c7a023 478793 70693 feb796e3 117a023
  //   478593 658663 482703 fc9ff06f 11400413 7c40913 100793 c0006f 4a783 448493 42503 440413 40f50533
  //   153513 f4dff0ef fe8912e3 100513 f41ff0ef c12083 812403 412483 12903 513 1010113 8067 18a02823 6f
  //   ff010113 11000513 112623 f25ff0ef 18a02823 6f 0 1 1e 1b3 fdc 6b0d 22caa 90f6f 1f1058 594efd da4f4e
  //   1ca7357 3418be4 527c829 72363ea 8aaf953 93ee7d0 8aaf953 72363ea 527c829 3418be4 1ca7357 da4f4e
  //   594efd 1f1058 90f6f 22caa 6b0d fdc 1b3 1e 1 2 3 4 5 6 7 8 9 a b c d e f 10 11 12 13 14 15 16 17 18
  //   19 1a 1b 1c 1d 1e 1f deadbeef deadbeef 444*0 413 9117 ffc10113 39c000ef 50463 8067 ff010113 100513
  //   112623 380000ef 259693 d506b3 50893 6a803 60513 6c5dc63 261793 f887b3 7a783 fff50613 261613 c88633
  //   140006f fff50513 472783 6b50863 70613 ffc60713 fef846e3 259693 d886b3 251313 f6a023 688633 4a5de63
  //   68713 c0006f 158593 2a58463 72783 70693 470713 fef856e3 f62023 f8a5cee3 58513 106a023 8067 6886b3
  //   6a783 f62023 106a023 8067 251693 d886b3 f6a023 fe9ff06f 58513 fe1ff06f 1ec5da63 fa010113 4812c23
  //   5612023 3812c23 4112e23 4912a23 5212823 5312623 5412423 5512223 3712e23 3912a23 3a12823 3b12623
  //   58c13 60b13 50413 b0613 c0593 40513 ee9ff0ef a12223 fff50c93 159c5663 c8613 c0593 40513 ecdff0ef
  //   a12423 fff50d13 13ac5263 d0613 c0593 40513 eb1ff0ef a12623 fff50d93 fbc5e63 d8613 c0593 40513
  //   e95ff0ef a12823 fff50993 d3c5a63 98613 c0593 40513 e79ff0ef fff50913 50493 b2c5863 90613 c0593 40513
  //   e5dff0ef fff50b93 50a13 97c5663 b8613 c0593 40513 e41ff0ef a12a23 fff50a93 75c5263 a8613 c0593 40513
  //   e25ff0ef fff50693 50713 4dc5063 68613 c0593 40513 e12e23 d12c23 e01ff0ef 50813 c0593 fff50613 40513
  //   180c13 eadff0ef 1812683 1c12703 fcdc44e3 170c13 fb5c42e3 1412783 178c13 f77c4ee3 1a0c13 f52c4ce3
  //   148c13 f33c4ae3 1012783 178c13 f1bc46e3 c12783 178c13 efac42e3 812783 178c13 eb9c4ee3 412783 178c13
  //   e96c4ae3 5c12083 5812403 5412483 5012903 4c12983 4812a03 4412a83 4012b03 3c12b83 3812c03 3412c83
  //   3012d03 2c12d83 6010113 8067 8067 fe010113 1412423 1300613 593 3c000513 812c23 912a23 1212823
  //   1312623 112e23 3c000493 dddff0ef 3c000913 413 1400993 92503 490913 40850533 153513 140413 cddff0ef
  //   ff3414e3 100513 cd1ff0ef 1300613 593 3c000513 d9dff0ef 413 1400913 4a503 448493 40850533 153513
  //   140413 ca1ff0ef ff2414e3 100513 c95ff0ef 1c12083 1812403 1412483 1012903 c12983 812a03 513 2010113
  //   8067 6f ff010113 3bc00513 112623 f31ff0ef 6f 0 2 c e 6 d f 10 a 0 12 b 13 9 1 7 5 4 3 8 11 deadbeef
  //   deadbeef 63658*0 413 9117 ffc10113 39c000ef 50463 8067 ff010113 100513 112623 380000ef 259693 d506b3
  //   50893 6a803 60513 6c5dc63 261793 f887b3 7a783 fff50613 261613 c88633 140006f fff50513 472783 6b50863
  //   70613 ffc60713 fef846e3 259693 d886b3 251313 f6a023 688633 4a5de63 68713 c0006f 158593 2a58463 72783
  //   70693 470713 fef856e3 f62023 f8a5cee3 58513 106a023 8067 6886b3 6a783 f62023 106a023 8067 251693
  //   d886b3 f6a023 fe9ff06f 58513 fe1ff06f 1ec5da63 fa010113 4812c23 5612023 3812c23 4112e23 4912a23
  //   5212823 5312623 5412423 5512223 3712e23 3912a23 3a12823 3b12623 58c13 60b13 50413 b0613 c0593 40513
  //   ee9ff0ef a12223 fff50c93 159c5663 c8613 c0593 40513 ecdff0ef a12423 fff50d13 13a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
endmodule

module \控制器  (
  input  [6:0] opcode,
  input  [2:0] funct3,
  input  [6:0] funct7,
  output [2:0] ExtOp,
  output RegWr,
  output [2:0] BandJ,
  output ALUASrc,
  output [1:0] ALUBSrc,
  output [3:0] ALUctr,
  output MemtoReg,
  output [2:0] MemOp,
  output MemWr,
  output Halt
);

  wire and_1_out, and_2_out, and_3_out, and_4_out, and_5_out, and_6_out, and_7_out, and_8_out, and_9_out,
       and_10_out, comparator_1_eq, comparator_2_eq, comparator_4_eq, comparator_5_eq, comparator_6_eq,
       comparator_11_eq, not_1_out, or_1_out, or_5_out, or_6_out, or_7_out, or_8_out, or_9_out;

  Comparator #(.width(7)) comparator_1 (.a(opcode), .b(7'b0110111), .eq(comparator_1_eq));  // open: gt, lt
  Comparator #(.width(7)) comparator_2 (.a(opcode), .b(7'b0010111), .eq(comparator_2_eq));  // open: gt, lt
  Comparator #(.width(7)) comparator_3 (.a(opcode), .b(7'b1101111), .eq(ExtOp[2]));  // open: gt, lt
  Comparator #(.width(7)) comparator_4 (.a(opcode), .b(7'b1100111), .eq(comparator_4_eq));  // open: gt, lt
  Comparator #(.width(7)) comparator_5 (.a(opcode), .b(7'b0010011), .eq(comparator_5_eq));  // open: gt, lt
  Comparator #(.width(7)) comparator_6 (.a(opcode), .b(7'b0110011), .eq(comparator_6_eq));  // open: gt, lt
  Comparator #(.width(7)) comparator_7 (.a(opcode), .b(7'b1100011), .eq(BandJ[2]));  // open: gt, lt
  Comparator #(.width(7)) comparator_8 (.a(opcode), .b(7'b0000011), .eq(MemtoReg));  // open: gt, lt
  Comparator #(.width(7)) comparator_9 (.a(opcode), .b(7'b0100011), .eq(MemWr));  // open: gt, lt
  Comparator #(.width(7)) comparator_10 (.a(opcode), .b({7{1'b0}}), .eq(Halt));  // open: gt, lt
  and and_1 (and_1_out, comparator_5_eq, funct3[0], ~funct3[1], funct3[2]);  // AND_Gate
  Comparator #(.width(7)) comparator_11 (.a({7{1'b0}}), .b(opcode), .eq(comparator_11_eq));  // open: gt, lt
  not not_1 (not_1_out, or_1_out);
  or or_1 (or_1_out, BandJ[2], MemWr);
  or or_2 (ALUASrc, comparator_2_eq, ExtOp[2], comparator_4_eq);
  or or_3 (ALUBSrc[0], ExtOp[2], comparator_4_eq);
  or or_4 (ALUBSrc[1], comparator_1_eq, comparator_2_eq, comparator_5_eq, MemtoReg, MemWr);
  and and_2 (and_2_out, BandJ[2], funct3[0]);
  and and_3 (and_3_out, BandJ[2], funct3[2]);
  and and_4 (and_4_out, comparator_5_eq, funct3[0]);
  and and_5 (and_5_out, comparator_6_eq, funct3[0]);
  and and_6 (and_6_out, BandJ[2], funct3[1]);
  and and_7 (and_7_out, comparator_5_eq, funct3[1]);
  and and_8 (and_8_out, comparator_6_eq, funct3[1]);
  and and_9 (and_9_out, funct3[2], or_5_out);
  or or_5 (or_5_out, comparator_5_eq, comparator_6_eq);
  and and_10 (and_10_out, funct7[5], or_6_out);
  or or_6 (or_6_out, and_1_out, comparator_6_eq);
  or or_7 (or_7_out, MemtoReg, MemWr);
  or or_8 (or_8_out, MemtoReg, MemWr);
  or or_9 (or_9_out, MemtoReg, MemWr);
  and and_11 (RegWr, ~comparator_11_eq, not_1_out);  // AND_Gate
  or or_10 (ExtOp[0], comparator_1_eq, comparator_2_eq, BandJ[2]);
  or or_11 (ExtOp[1], BandJ[2], MemWr);
  or or_12 (BandJ[0], ExtOp[2], and_2_out);
  or or_13 (BandJ[1], comparator_4_eq, and_3_out);
  or or_14 (ALUctr[0], comparator_1_eq, and_4_out, and_5_out, and_6_out);
  or or_15 (ALUctr[1], comparator_1_eq, and_7_out, and_8_out, BandJ[2]);
  or or_16 (ALUctr[2], comparator_1_eq, and_9_out);
  or or_17 (ALUctr[3], comparator_1_eq, and_10_out);
  and and_12 (MemOp[0], ~funct3[0], ~funct3[1], or_7_out);  // AND_Gate
  and and_13 (MemOp[1], funct3[0], or_8_out);
  and and_14 (MemOp[2], ~funct3[1], ~funct3[2], or_9_out);  // AND_Gate

  // Notes on the sheet:
  //   输入引脚
  //   U-lui
  //   U-auipc
  //   J-jal
  //   J-jalr
  //   I-Arith
  //   R-Arith
  //   B-Instr
  //   I-load
  //   S-Instr
  //   halt
  //   请勿修改引脚名称、电路名称及电路封装外观
  //   提示：根据指令种类，把7位指令code用一位指令类型标志位来表示，再通过功能码来区分具体指令，生成控制信号。
  //   输出引脚
endmodule

module IDU (
  input  [31:0] IR,
  input  [31:0] BusW,
  input  [31:0] PC,
  input  [2:0] ExtOp,
  input  RegWr,
  input  ALUASrc,
  input  [1:0] ALUBSrc,
  input  CLK,
  output [31:0] DataA,
  output [31:0] DataB,
  output [31:0] BusA,
  output [31:0] BusB,
  output [6:0] OpCode,
  output [31:0] Imm,
  output [2:0] Funct3,
  output [6:0] Funct7
);

  \立即数扩展器  \u_立即数扩展器_1  (.Instr(IR), .Extop(ExtOp), .imm(Imm));
  RegFile regfile_1 (
    .R1_num(IR[19:15]), .R2_num(IR[24:20]), .Write_Reg_num(IR[11:7]), .Write_Enable(RegWr), .Clock(CLK),
    .Din(BusW), .Reg1Out(BusA), .Reg2Out(BusB));
  Multiplexer #(.width(32), .enable("false")) multiplexer_1 (.in0(BusA), .in1(PC), .out(DataA), .sel(ALUASrc));
  Multiplexer #(.select(2), .width(32), .enable("false")) multiplexer_2 (
    .in0(BusB), .in1(32'h4), .in2(Imm), .out(DataB), .sel(ALUBSrc));  // open: in3

  assign Funct3 = IR[14:12];
  assign Funct7 = IR[31:25];
  assign OpCode = IR[6:0];

  // Other names for the same wires on the sheet: op[6:0] = IR[6:0]

  // Notes on the sheet:
  //   BusW: pull=down
  //   ALUBSrc: pull=down
  //   RegWr: pull=down
  //   ALUASrc: pull=down
  //   ExtOp: pull=down
  //   PC: pull=down
  //   输入信号
  //   为了后续实验中的引用，不要修改ALUASrc、ALUBSrc和EXtOP编码定义。
  //   请勿修改引脚名称、电路名称及电路封装外观
  //   输出信号
  //   修改寄存器堆电路设计，0号寄存器始终为0。
endmodule

module RegFile (
  input  [4:0] R1_num,
  input  [4:0] R2_num,
  input  [4:0] Write_Reg_num,
  input  [31:0] Din,
  input  Write_Enable,
  input  Clock,
  output [31:0] Reg1Out,
  output [31:0] Reg2Out
);

  wire and_1_out, and_2_out, and_3_out, and_4_out, and_5_out, and_6_out, and_7_out, and_8_out, and_9_out,
       and_10_out, and_11_out, and_12_out, and_13_out, and_14_out, and_15_out, and_16_out, and_17_out,
       and_18_out, and_19_out, and_20_out, and_21_out, and_22_out, and_23_out, and_24_out, and_25_out,
       and_26_out, and_27_out, and_28_out, and_29_out, and_30_out, and_31_out, and_32_out, decoder_1_out0,
       decoder_1_out1, decoder_1_out2, decoder_1_out3, decoder_1_out4, decoder_1_out5, decoder_1_out6,
       decoder_1_out7, decoder_1_out8, decoder_1_out9, decoder_1_out10, decoder_1_out11, decoder_1_out12,
       decoder_1_out13, decoder_1_out14, decoder_1_out15, decoder_1_out16, decoder_1_out17, decoder_1_out18,
       decoder_1_out19, decoder_1_out20, decoder_1_out21, decoder_1_out22, decoder_1_out23, decoder_1_out24,
       decoder_1_out25, decoder_1_out26, decoder_1_out27, decoder_1_out28, decoder_1_out29, decoder_1_out30,
       decoder_1_out31;
  wire [31:0] _0_q, _1_q, _2_q, _3_q, _4_q, _5_q, _6_q, _7_q, _8_q, _9_q, register_1_q, register_2_q,
       register_3_q, register_4_q, register_5_q, register_6_q, register_7_q, register_8_q, register_9_q,
       register_10_q, register_11_q, register_12_q, register_13_q, register_14_q, register_15_q,
       register_16_q, register_17_q, register_18_q, register_19_q, register_20_q, register_21_q,
       register_22_q;

  Decoder #(.select(5), .enable("false")) decoder_1 (
    .out0(decoder_1_out0), .out1(decoder_1_out1), .out2(decoder_1_out2), .out3(decoder_1_out3),
    .out4(decoder_1_out4), .out5(decoder_1_out5), .out6(decoder_1_out6), .out7(decoder_1_out7),
    .out8(decoder_1_out8), .out9(decoder_1_out9), .out10(decoder_1_out10), .out11(decoder_1_out11),
    .out12(decoder_1_out12), .out13(decoder_1_out13), .out14(decoder_1_out14), .out15(decoder_1_out15),
    .out16(decoder_1_out16), .out17(decoder_1_out17), .out18(decoder_1_out18), .out19(decoder_1_out19),
    .out20(decoder_1_out20), .out21(decoder_1_out21), .out22(decoder_1_out22), .out23(decoder_1_out23),
    .out24(decoder_1_out24), .out25(decoder_1_out25), .out26(decoder_1_out26), .out27(decoder_1_out27),
    .out28(decoder_1_out28), .out29(decoder_1_out29), .out30(decoder_1_out30), .out31(decoder_1_out31),
    .sel(Write_Reg_num));
  and and_1 (and_1_out, Write_Enable, decoder_1_out0);
  and and_2 (and_2_out, Write_Enable, decoder_1_out1);
  and and_3 (and_3_out, Write_Enable, decoder_1_out2);
  and and_4 (and_4_out, Write_Enable, decoder_1_out3);
  and and_5 (and_5_out, Write_Enable, decoder_1_out4);
  and and_6 (and_6_out, Write_Enable, decoder_1_out5);
  and and_7 (and_7_out, Write_Enable, decoder_1_out6);
  and and_8 (and_8_out, Write_Enable, decoder_1_out7);
  and and_9 (and_9_out, Write_Enable, decoder_1_out8);
  and and_10 (and_10_out, Write_Enable, decoder_1_out9);
  and and_11 (and_11_out, Write_Enable, decoder_1_out10);
  and and_12 (and_12_out, Write_Enable, decoder_1_out11);
  and and_13 (and_13_out, Write_Enable, decoder_1_out12);
  and and_14 (and_14_out, Write_Enable, decoder_1_out13);
  and and_15 (and_15_out, Write_Enable, decoder_1_out14);
  and and_16 (and_16_out, Write_Enable, decoder_1_out15);
  and and_17 (and_17_out, Write_Enable, decoder_1_out16);
  and and_18 (and_18_out, Write_Enable, decoder_1_out17);
  and and_19 (and_19_out, Write_Enable, decoder_1_out18);
  and and_20 (and_20_out, Write_Enable, decoder_1_out19);
  and and_21 (and_21_out, Write_Enable, decoder_1_out20);
  and and_22 (and_22_out, Write_Enable, decoder_1_out21);
  and and_23 (and_23_out, Write_Enable, decoder_1_out22);
  and and_24 (and_24_out, Write_Enable, decoder_1_out23);
  and and_25 (and_25_out, Write_Enable, decoder_1_out24);
  and and_26 (and_26_out, Write_Enable, decoder_1_out25);
  and and_27 (and_27_out, Write_Enable, decoder_1_out26);
  and and_28 (and_28_out, Write_Enable, decoder_1_out27);
  and and_29 (and_29_out, Write_Enable, decoder_1_out28);
  and and_30 (and_30_out, Write_Enable, decoder_1_out29);
  and and_31 (and_31_out, Write_Enable, decoder_1_out30);
  and and_32 (and_32_out, Write_Enable, decoder_1_out31);
  Register #(.width(32), .Select("high")) _0 (.D({32{1'b0}}), .en(and_1_out), .Q(_0_q), .clk(Clock));  // open: clr
  Register #(.width(32), .Select("high")) _1 (.D(Din), .en(and_2_out), .Q(_1_q), .clk(Clock));  // open: clr
  Register #(.width(32), .Select("high")) _2 (.D(Din), .en(and_3_out), .Q(_2_q), .clk(Clock));  // open: clr
  Register #(.width(32), .Select("high")) _3 (.D(Din), .en(and_4_out), .Q(_3_q), .clk(Clock));  // open: clr
  Register #(.width(32), .Select("high")) _4 (.D(Din), .en(and_5_out), .Q(_4_q), .clk(Clock));  // open: clr
  Register #(.width(32), .Select("high")) _5 (.D(Din), .en(and_6_out), .Q(_5_q), .clk(Clock));  // open: clr
  Register #(.width(32), .Select("high")) _6 (.D(Din), .en(and_7_out), .Q(_6_q), .clk(Clock));  // open: clr
  Register #(.width(32), .Select("high")) _7 (.D(Din), .en(and_8_out), .Q(_7_q), .clk(Clock));  // open: clr
  Register #(.width(32), .Select("high")) _8 (.D(Din), .en(and_9_out), .Q(_8_q), .clk(Clock));  // open: clr
  Register #(.width(32), .Select("high")) _9 (.D(Din), .en(and_10_out), .Q(_9_q), .clk(Clock));  // open: clr
  Register #(.width(32), .Select("high")) register_1 (
    .D(Din), .en(and_11_out), .Q(register_1_q), .clk(Clock));  // open: clr
  Register #(.width(32), .Select("high")) register_2 (
    .D(Din), .en(and_12_out), .Q(register_2_q), .clk(Clock));  // open: clr
  Register #(.width(32), .Select("high")) register_3 (
    .D(Din), .en(and_13_out), .Q(register_3_q), .clk(Clock));  // open: clr
  Register #(.width(32), .Select("high")) register_4 (
    .D(Din), .en(and_14_out), .Q(register_4_q), .clk(Clock));  // open: clr
  Register #(.width(32), .Select("high")) register_5 (
    .D(Din), .en(and_15_out), .Q(register_5_q), .clk(Clock));  // open: clr
  Register #(.width(32), .Select("high")) register_6 (
    .D(Din), .en(and_16_out), .Q(register_6_q), .clk(Clock));  // open: clr
  Register #(.width(32), .Select("high")) register_7 (
    .D(Din), .en(and_17_out), .Q(register_7_q), .clk(Clock));  // open: clr
  Register #(.width(32), .Select("high")) register_8 (
    .D(Din), .en(and_18_out), .Q(register_8_q), .clk(Clock));  // open: clr
  Register #(.width(32), .Select("high")) register_9 (
    .D(Din), .en(and_19_out), .Q(register_9_q), .clk(Clock));  // open: clr
  Register #(.width(32), .Select("high")) register_10 (
    .D(Din), .en(and_20_out), .Q(register_10_q), .clk(Clock));  // open: clr
  Register #(.width(32), .Select("high")) register_11 (
    .D(Din), .en(and_21_out), .Q(register_11_q), .clk(Clock));  // open: clr
  Register #(.width(32), .Select("high")) register_12 (
    .D(Din), .en(and_22_out), .Q(register_12_q), .clk(Clock));  // open: clr
  Register #(.width(32), .Select("high")) register_13 (
    .D(Din), .en(and_23_out), .Q(register_13_q), .clk(Clock));  // open: clr
  Register #(.width(32), .Select("high")) register_14 (
    .D(Din), .en(and_24_out), .Q(register_14_q), .clk(Clock));  // open: clr
  Register #(.width(32), .Select("high")) register_15 (
    .D(Din), .en(and_25_out), .Q(register_15_q), .clk(Clock));  // open: clr
  Register #(.width(32), .Select("high")) register_16 (
    .D(Din), .en(and_26_out), .Q(register_16_q), .clk(Clock));  // open: clr
  Register #(.width(32), .Select("high")) register_17 (
    .D(Din), .en(and_27_out), .Q(register_17_q), .clk(Clock));  // open: clr
  Register #(.width(32), .Select("high")) register_18 (
    .D(Din), .en(and_28_out), .Q(register_18_q), .clk(Clock));  // open: clr
  Register #(.width(32), .Select("high")) register_19 (
    .D(Din), .en(and_29_out), .Q(register_19_q), .clk(Clock));  // open: clr
  Register #(.width(32), .Select("high")) register_20 (
    .D(Din), .en(and_30_out), .Q(register_20_q), .clk(Clock));  // open: clr
  Register #(.width(32), .Select("high")) register_21 (
    .D(Din), .en(and_31_out), .Q(register_21_q), .clk(Clock));  // open: clr
  Register #(.width(32), .Select("high")) register_22 (
    .D(Din), .en(and_32_out), .Q(register_22_q), .clk(Clock));  // open: clr
  Multiplexer #(.select(5), .width(32), .enable("false")) multiplexer_1 (
    .in0(_0_q), .in1(_1_q), .in2(_2_q), .in3(_3_q), .in4(_4_q), .in5(_5_q), .in6(_6_q), .in7(_7_q),
    .in8(_8_q), .in9(_9_q), .in10(register_1_q), .in11(register_2_q), .in12(register_3_q),
    .in13(register_4_q), .in14(register_5_q), .in15(register_6_q), .in16(register_7_q), .in17(register_8_q),
    .in18(register_9_q), .in19(register_10_q), .in20(register_11_q), .in21(register_12_q),
    .in22(register_13_q), .in23(register_14_q), .in24(register_15_q), .in25(register_16_q),
    .in26(register_17_q), .in27(register_18_q), .in28(register_19_q), .in29(register_20_q),
    .in30(register_21_q), .in31(register_22_q), .out(Reg1Out), .sel(R1_num));
  Multiplexer #(.select(5), .width(32), .enable("false")) multiplexer_2 (
    .in0(_0_q), .in1(_1_q), .in2(_2_q), .in3(_3_q), .in4(_4_q), .in5(_5_q), .in6(_6_q), .in7(_7_q),
    .in8(_8_q), .in9(_9_q), .in10(register_1_q), .in11(register_2_q), .in12(register_3_q),
    .in13(register_4_q), .in14(register_5_q), .in15(register_6_q), .in16(register_7_q), .in17(register_8_q),
    .in18(register_9_q), .in19(register_10_q), .in20(register_11_q), .in21(register_12_q),
    .in22(register_13_q), .in23(register_14_q), .in24(register_15_q), .in25(register_16_q),
    .in26(register_17_q), .in27(register_18_q), .in28(register_19_q), .in29(register_20_q),
    .in30(register_21_q), .in31(register_22_q), .out(Reg2Out), .sel(R2_num));

  // Other names for the same wires on the sheet: CLK = Clock; RA[4:0] = R1_num; RB[4:0] = R2_num; RDA[31:0] = Reg1Out;
  //   RDB[31:0] = Reg2Out; RW[4:0] = Write_Reg_num; WE = Write_Enable

  // Notes on the sheet:
  //   输入引脚
  //   请勿修改引脚名称、电路名称及电路封装外观
  //   提示：使用译码器、多路选择器和32位寄存器及逻辑门实现寄存器堆，禁止直接使用存储器组件。
  //   输出引脚
endmodule

module \立即数扩展器  (
  input  [31:0] Instr,
  input  [2:0] Extop,
  output [31:0] imm
);

  wire [11:0] bit_extender_4_out;
  wire [19:0] bit_extender_3_out;
  wire [26:0] bit_extender_2_out;
  wire [31:0] bit_extender_1_out;

  assign bit_extender_1_out = {{20{Instr[31]}}, Instr[31:20]};  // Bit_Extender bit_extender_1
  assign bit_extender_2_out = {{20{Instr[31]}}, Instr[31:25]};  // Bit_Extender bit_extender_2
  assign bit_extender_3_out = {{19{Instr[31]}}, Instr[31]};  // Bit_Extender bit_extender_3
  assign bit_extender_4_out = {{11{Instr[31]}}, Instr[31]};  // Bit_Extender bit_extender_4
  Multiplexer #(.select(3), .width(32), .enable("false")) multiplexer_1 (
    .in0(bit_extender_1_out), .in1({Instr[31:12], {12{1'b0}}}), .in2({bit_extender_2_out, Instr[11:7]}),
    .in3({bit_extender_3_out, Instr[7], Instr[30:25], Instr[11:8], 1'b0}),
    .in4({bit_extender_4_out, Instr[19:12], Instr[20], Instr[30:21], 1'b0}), .out(imm), .sel(Extop));  // open: in5, in6, in7

  // Notes on the sheet:
  //   Instr: pull=down
  //   Extop: pull=down
  //   输入引脚
  //   输出引脚
endmodule

module DataRAM (
  input  CLK,
  input  CLR,
  input  WE,
  input  [2:0] MemOp,
  input  [17:0] Addr,
  input  [31:0] Din,
  output AlignErr,
  output [31:0] DataOut
);

  wire and_3_out, and_4_out, and_5_out, and_6_out, and_7_out, and_8_out, and_9_out, and_10_out, and_11_out,
       and_12_out, and_13_out, or_1_out, or_2_out, or_3_out, or_4_out, or_5_out, or_6_out, or_7_out;
  wire [1:0] and_2_out;
  wire [7:0] multiplexer_1_out, multiplexer_2_out, multiplexer_3_out, multiplexer_5_out, ram_3_data,
       ram_4_data;
  wire [15:0] multiplexer_4_out, ram_1_data;
  wire [31:0] bit_extender_1_out, bit_extender_2_out, bit_extender_3_out, bit_extender_4_out;

  and and_1 (and_2_out[1], ~MemOp[0], ~MemOp[1], ~MemOp[2]);  // AND_Gate
  and and_2 (and_2_out[0], ~MemOp[0], MemOp[1], MemOp[2]);  // AND_Gate
  and and_3 (and_3_out, MemOp[0], ~MemOp[1], MemOp[2]);  // AND_Gate
  Multiplexer #(.width(8), .enable("false")) multiplexer_1 (
    .in0(Din[7:0]), .in1(Din[15:8]), .out(multiplexer_1_out), .sel(or_2_out));
  RAM #(.addrWidth(18), .bus("separate"), .Select("high")) ram_1 (
    .addr({Addr[17:2], 2'b00}), .din(Din[7:0]), .data(ram_1_data[7:0]), .str(and_13_out), .sel(or_4_out),
    .clk(CLK), .ld(or_4_out), .clr(CLR));
  RAM #(.addrWidth(18), .bus("separate"), .Select("high")) ram_2 (
    .addr({Addr[17:2], 2'b00}), .din(multiplexer_1_out), .data(ram_1_data[15:8]), .str(and_13_out),
    .sel(or_5_out), .clk(CLK), .ld(or_5_out), .clr(CLR));
  or or_1 (or_1_out, and_2_out[1], and_2_out[0], and_3_out);
  Multiplexer #(.width(8), .enable("false")) multiplexer_2 (
    .in0(Din[7:0]), .in1(Din[23:16]), .out(multiplexer_2_out), .sel(and_2_out[1]));
  and and_4 (and_4_out, ~Addr[0], ~MemOp[0], MemOp[1]);  // AND_Gate
  and and_5 (and_5_out, MemOp[0], ~MemOp[1]);  // AND_Gate
  or or_2 (or_2_out, and_2_out[1], and_2_out[0]);
  and and_6 (and_6_out, ~Addr[0], ~Addr[1], ~MemOp[2], ~MemOp[0], ~MemOp[1]);  // AND_Gate
  and and_7 (and_7_out, ~Addr[0], ~Addr[1], MemOp[0], ~MemOp[1]);  // AND_Gate
  and and_8 (and_8_out, Addr[0], ~Addr[1], MemOp[0], ~MemOp[1]);  // AND_Gate
  and and_9 (and_9_out, ~Addr[0], Addr[1], MemOp[0], ~MemOp[1]);  // AND_Gate
  and and_10 (and_10_out, Addr[0], Addr[1], MemOp[0], ~MemOp[1]);  // AND_Gate
  and and_11 (and_11_out, ~Addr[0], ~Addr[1], ~MemOp[0], MemOp[1]);  // AND_Gate
  and and_12 (and_12_out, ~Addr[0], Addr[1], ~MemOp[0], MemOp[1]);  // AND_Gate
  RAM #(.addrWidth(18), .bus("separate"), .Select("high")) ram_3 (
    .addr({Addr[17:2], 2'b00}), .din(multiplexer_2_out), .data(ram_3_data), .str(and_13_out), .sel(or_6_out),
    .clk(CLK), .ld(or_6_out), .clr(CLR));
  Multiplexer #(.select(2), .width(8), .enable("false")) multiplexer_3 (
    .in0(Din[7:0]), .in1(Din[15:8]), .in2(Din[31:24]), .out(multiplexer_3_out), .sel(and_2_out));  // open: in3
  not not_1 (AlignErr, or_3_out);
  or or_3 (or_3_out, and_4_out, and_5_out, and_6_out);
  or or_4 (or_4_out, and_6_out, and_7_out, and_11_out);
  or or_5 (or_5_out, and_6_out, and_8_out, and_11_out);
  or or_6 (or_6_out, and_6_out, and_9_out, and_12_out);
  or or_7 (or_7_out, and_6_out, and_10_out, and_12_out);
  and and_13 (and_13_out, or_1_out, WE);
  RAM #(.addrWidth(18), .bus("separate"), .Select("high")) ram_4 (
    .addr({Addr[17:2], 2'b00}), .din(multiplexer_3_out), .data(ram_4_data), .str(and_13_out), .sel(or_7_out),
    .clk(CLK), .ld(or_7_out), .clr(CLR));
  Multiplexer #(.width(16), .enable("false")) multiplexer_4 (
    .in0(ram_1_data), .in1({ram_4_data, ram_3_data}), .out(multiplexer_4_out), .sel(Addr[1]));
  Multiplexer #(.select(2), .width(8), .enable("false")) multiplexer_5 (
    .in0(ram_1_data[7:0]), .in1(ram_1_data[15:8]), .in2(ram_3_data), .in3(ram_4_data),
    .out(multiplexer_5_out), .sel(Addr[1:0]));
  assign bit_extender_1_out = {{16{1'b0}}, multiplexer_4_out};  // Bit_Extender bit_extender_1
  assign bit_extender_2_out = {{16{multiplexer_4_out[15]}}, multiplexer_4_out};  // Bit_Extender bit_extender_2
  assign bit_extender_3_out = {{24{1'b0}}, multiplexer_5_out};  // Bit_Extender bit_extender_3
  assign bit_extender_4_out = {{24{multiplexer_5_out[7]}}, multiplexer_5_out};  // Bit_Extender bit_extender_4
  Multiplexer #(.select(3), .width(32), .enable("false")) multiplexer_6 (
    .in0({ram_4_data, ram_3_data, ram_1_data}), .in1(bit_extender_3_out), .in2(bit_extender_1_out),
    .in5(bit_extender_4_out), .in6(bit_extender_2_out), .out(DataOut), .sel(MemOp));  // open: in3, in4, in7

  // Other names for the same wires on the sheet: Dout[31:0] = DataOut

  // Notes on the sheet:
  //   输入引脚
  //   请勿修改引脚名称、电路名称及电路封装外观
  //   为了后续实验中的引用，不要修改MemOp的编码定义、引脚名称和在布局中的位置。
  //   32位数据存储器，按字节分4片存储，可按照字节、半字和字进行存储；读取字节或半字时，支持0扩展和符号位扩展。
  //   输出引脚
endmodule

module ALU (
  input  [3:0] ALUctr,
  input  [31:0] A,
  input  [31:0] B,
  output Zero,
  output [31:0] S
);

  wire adder32_1_cout, adder32_1_of, adder32_1_sf, aluctrl_1_alctr, aluctrl_1_sftctr, aluctrl_1_sigctr,
       aluctrl_1_subctr, multiplexer_2_out, xor_3_out, xor_4_out;
  wire [2:0] aluctrl_1_opctr;
  wire [31:0] adder32_1_s, and_1_out, bit_extender_1_out, bit_extender_2_out, or_1_out, shifter32_1_dataout,
       xor_1_out, xor_2_out;

  assign bit_extender_1_out = {{31{aluctrl_1_subctr}}, aluctrl_1_subctr};  // Bit_Extender bit_extender_1
  assign and_1_out = A & B;  // AND_Gate and_1, 32 bits wide
  assign or_1_out = A | B;  // OR_Gate or_1, 32 bits wide
  assign xor_1_out = B ^ bit_extender_1_out;  // XOR_Gate xor_1, 32 bits wide
  assign xor_2_out = A ^ B;  // XOR_Gate xor_2, 32 bits wide
  Shifter32 shifter32_1 (
    .DataIn(A), .shamt(B[4:0]), .L_R(aluctrl_1_sftctr), .A_L(aluctrl_1_alctr), .DataOut(shifter32_1_dataout));
  Adder32 adder32_1 (
    .OF(adder32_1_of), .SF(adder32_1_sf), .ZF(Zero), .X(A), .Y(xor_1_out), .Cin(aluctrl_1_subctr),
    .S(adder32_1_s), .Cout(adder32_1_cout));  // open: CF
  ALUctrl aluctrl_1 (
    .SUBctr(aluctrl_1_subctr), .SFTctr(aluctrl_1_sftctr), .SIGctr(aluctrl_1_sigctr), .ALctr(aluctrl_1_alctr),
    .OPctr(aluctrl_1_opctr), .ALUctr(ALUctr));
  xor xor_3 (xor_3_out, aluctrl_1_subctr, adder32_1_cout);
  xor xor_4 (xor_4_out, adder32_1_of, adder32_1_sf);
  Multiplexer #(.select(3), .width(32), .enable("false")) multiplexer_1 (
    .in0(adder32_1_s), .in1(and_1_out), .in2(or_1_out), .in3(xor_2_out), .in4(shifter32_1_dataout), .in5(B),
    .in6(bit_extender_2_out), .out(S), .sel(aluctrl_1_opctr));  // open: in7
  // Probe on A
  // Probe on B
  // Probe on S
  Multiplexer #(.enable("false")) multiplexer_2 (
    .in0(xor_3_out), .in1(xor_4_out), .out(multiplexer_2_out), .sel(aluctrl_1_sigctr));
  assign bit_extender_2_out = {{31{1'b0}}, multiplexer_2_out};  // Bit_Extender bit_extender_2

  // Other names for the same wires on the sheet: Result[31:0] = S

  // Notes on the sheet:
  //   ALUctr: pull=down
  //   A: pull=down
  //   B: pull=down
  //   输入引脚
  //   请勿修改引脚名称、电路名称及电路封装外观
  //   提示：使用32位并行加法器子电路、桶形移位器、ALU控制子电路实现32位ALU
  //   功能说明:32位ALU，输入32位操作数A、B，4位控制信号ALUctr，输出32位结果Reseult和1位Zero标志位
  //   输出引脚
  //   操作数和结果
endmodule

module ALUctrl (
  input  [3:0] ALUctr,
  output SUBctr,
  output SFTctr,
  output SIGctr,
  output ALctr,
  output [2:0] OPctr
);

  wire and_2_out, and_3_out, and_6_out, and_7_out, and_8_out, and_9_out, and_10_out, and_11_out, and_12_out;

  and and_1 (SIGctr, ~ALUctr[0], ALUctr[1], ~ALUctr[2], ~ALUctr[3]);  // AND_Gate
  and and_2 (and_2_out, ALUctr[1], ~ALUctr[2], ~ALUctr[3]);  // AND_Gate
  and and_3 (and_3_out, ~ALUctr[0], ~ALUctr[1], ~ALUctr[2], ALUctr[3]);  // AND_Gate
  and and_4 (SFTctr, ALUctr[0], ~ALUctr[1], ~ALUctr[2], ~ALUctr[3]);  // AND_Gate
  and and_5 (ALctr, ALUctr[0], ~ALUctr[1], ALUctr[3], ALUctr[2]);  // AND_Gate
  and and_6 (and_6_out, ALUctr[1], ~ALUctr[2], ~ALUctr[3]);  // AND_Gate
  and and_7 (and_7_out, ALUctr[0], ~ALUctr[1], ~ALUctr[3]);  // AND_Gate
  and and_8 (and_8_out, ALUctr[0], ALUctr[2], ALUctr[3]);
  and and_9 (and_9_out, ALUctr[1], ~ALUctr[2], ~ALUctr[3]);  // AND_Gate
  and and_10 (and_10_out, ~ALUctr[0], ALUctr[2], ~ALUctr[3]);  // AND_Gate
  and and_11 (and_11_out, ALUctr[0], ALUctr[1], ALUctr[2]);
  and and_12 (and_12_out, ~ALUctr[0], ~ALUctr[1], ALUctr[2], ~ALUctr[3]);  // AND_Gate
  or or_1 (SUBctr, and_2_out, and_3_out);
  or or_2 (OPctr[2], and_6_out, and_7_out, and_8_out);
  or or_3 (OPctr[1], and_9_out, and_10_out);
  or or_4 (OPctr[0], and_11_out, and_12_out);

  // Other names for the same wires on the sheet: LRctr = SFTctr

  // Notes on the sheet:
  //   输入引脚
  //   ALU操作控制信号生成部件
  //   ALU操作控制信号生成部件
  //   输出引脚
endmodule

module Adder32 (
  input  Cin,
  input  [31:0] X,
  input  [31:0] Y,
  output CF,
  output Cout,
  output OF,
  output SF,
  output [31:0] S,
  output ZF
);

  wire adder16_1_pg, adder16_2_c16, adder16_2_pg, and_1_out, and_2_out;

  xor xor_1 (CF, Cin, Cout);
  Adder16 adder16_1 (
    .X(X[31:16]), .Y(Y[31:16]), .C0(adder16_2_c16), .S(S[31:16]), .C16(Cout), .Pg(adder16_1_pg),
    .Gg(adder16_1_pg));
  Adder16 adder16_2 (
    .X(X[15:0]), .Y(Y[15:0]), .C0(Cin), .S(S[15:0]), .C16(adder16_2_c16), .Pg(adder16_2_pg), .Gg(adder16_2_pg));
  // Probe on X
  // Probe on Y
  // Probe on S
  and and_1 (and_1_out, Y[31], X[31], ~S[31]);  // AND_Gate
  and and_2 (and_2_out, ~Y[31], ~X[31], S[31]);  // AND_Gate
  or or_1 (OF, and_1_out, and_2_out);
  Comparator #(.width(32)) comparator_1 (.a(S), .b({32{1'b0}}), .eq(ZF));  // open: gt, lt

  assign SF = S[31];
  // also tied to GND on the sheet: {adder16_1_pg, adder16_2_pg}

  // Notes on the sheet:
  //   X: pull=down
  //   Cin: pull=down
  //   Y: pull=down
  //   输入引脚区
  //   输出引脚区
  //   请勿修改引脚名称、电路名称及电路封装外观
  //   提示：使用16位并行加法器子电路实现32位快速加法器
  //   功能说明:32位Adder  S=X+Y，Cout为最高位进位位，Cin为进位输入， S为和，溢出OF、进位CF、零ZF、符号SF。
  //   +
  //   =
  //   无符号加法
endmodule

// 移位器
module Shifter32 (
  input  [4:0] shamt,
  input  L_R,
  input  A_L,
  input  [31:0] DataIn,
  output [31:0] DataOut
);

  wire [14:0] multiplexer_7_out;
  wire [15:15] multiplexer_7_out_2;
  wire [31:0] multiplexer_1_out, multiplexer_2_out, multiplexer_3_out, multiplexer_4_out, multiplexer_5_out,
       multiplexer_6_out, multiplexer_8_out, multiplexer_10_out;
  wire [31:16] multiplexer_7_out_3;

  Multiplexer #(.width(32), .enable("false")) multiplexer_1 (
    .in0(DataIn), .in1(multiplexer_2_out), .out(multiplexer_1_out), .sel(shamt[0]));
  Multiplexer #(.select(2), .width(32), .enable("false")) multiplexer_2 (
    .in0({1'b0, DataIn[31:1]}), .in1({{2{DataIn[31]}}, DataIn[30:1]}), .in2({DataIn[30:0], 1'b0}),
    .in3({DataIn[30:0], DataIn[31]}), .out(multiplexer_2_out), .sel({L_R, A_L}));
  Multiplexer #(.width(32), .enable("false")) multiplexer_3 (
    .in0(multiplexer_1_out), .in1(multiplexer_4_out), .out(multiplexer_3_out), .sel(shamt[1]));
  Multiplexer #(.select(2), .width(32), .enable("false")) multiplexer_4 (
    .in0({2'b00, multiplexer_1_out[31:2]}), .in1({{3{multiplexer_1_out[31]}}, multiplexer_1_out[30:2]}),
    .in2({multiplexer_1_out[29:0], 2'b00}), .in3({multiplexer_1_out[29:0], multiplexer_1_out[31:30]}),
    .out(multiplexer_4_out), .sel({L_R, A_L}));
  Multiplexer #(.width(32), .enable("false")) multiplexer_5 (
    .in0(multiplexer_3_out), .in1(multiplexer_6_out), .out(multiplexer_5_out), .sel(shamt[2]));
  Multiplexer #(.select(2), .width(32), .enable("false")) multiplexer_6 (
    .in0({4'b0000, multiplexer_3_out[31:4]}), .in1({{5{multiplexer_3_out[31]}}, multiplexer_3_out[30:4]}),
    .in2({multiplexer_3_out[27:0], 4'b0000}), .in3({multiplexer_3_out[27:0], multiplexer_3_out[31:28]}),
    .out(multiplexer_6_out), .sel({L_R, A_L}));
  Multiplexer #(.width(32), .enable("false")) multiplexer_7 (
    .in0(multiplexer_5_out), .in1(multiplexer_8_out),
    .out({multiplexer_7_out_2[15], multiplexer_7_out, multiplexer_7_out_3}), .sel(shamt[3]));
  Multiplexer #(.select(2), .width(32), .enable("false")) multiplexer_8 (
    .in0({{8{1'b0}}, multiplexer_5_out[31:8]}), .in1({{9{multiplexer_5_out[31]}}, multiplexer_5_out[30:8]}),
    .in2({multiplexer_5_out[23:0], {8{1'b0}}}), .in3({multiplexer_5_out[23:0], multiplexer_5_out[31:24]}),
    .out(multiplexer_8_out), .sel({L_R, A_L}));
  Multiplexer #(.width(32), .enable("false")) multiplexer_9 (
    .in0({multiplexer_7_out_2[15], multiplexer_7_out, multiplexer_7_out_3}), .in1(multiplexer_10_out),
    .out(DataOut), .sel(shamt[4]));
  Multiplexer #(.select(2), .width(32), .enable("false")) multiplexer_10 (
    .in0({{16{1'b0}}, multiplexer_7_out_2[15], multiplexer_7_out}),
    .in1({{17{multiplexer_7_out_2[15]}}, multiplexer_7_out}), .in2({multiplexer_7_out_3, {16{1'b0}}}),
    .in3({multiplexer_7_out_3, multiplexer_7_out_2[15], multiplexer_7_out}), .out(multiplexer_10_out),
    .sel({L_R, A_L}));

  // Other names for the same wires on the sheet: Din[31:0] = DataIn; Arth_Logic = A_L; Left_Right = L_R;
  //   Dout[31:0] = DataOut

  // Notes on the sheet:
  //   L/R,A/L: 00逻辑右移，01算术右移，10逻辑左移，11：循环左移
  //   输入引脚
  //   请勿修改引脚名称、电路名称及电路封装外观
  //   提示：使用多路选择器、逻辑门实现32位桶形移位器，禁止直接使用移位器组件。
  //   输出引脚
endmodule

module Adder16 (
  input  C0,
  input  [15:0] X,
  input  [15:0] Y,
  output C16,
  output Pg,
  output Gg,
  output [15:0] S
);

  wire cla4_1_gg, cla4_1_pg, cla4_2_gg, cla4_2_pg, cla4_3_gg, cla4_3_pg, cla4_4_gg, cla4_4_pg, clu4_1_c1,
       clu4_1_c2, clu4_1_c3;

  CLA4 cla4_1 (.X(X[15:12]), .F(S[15:12]), .Cout(C16), .Y(Y[15:12]), .Pg(cla4_1_pg), .Cin(clu4_1_c3), .Gg(cla4_1_gg));
  CLA4 cla4_2 (.X(X[11:8]), .F(S[11:8]), .Y(Y[11:8]), .Pg(cla4_2_pg), .Cin(clu4_1_c2), .Gg(cla4_2_gg));  // open: Cout
  CLU4 clu4_1 (
    .P0(cla4_4_pg), .P1(cla4_3_pg), .P2(cla4_2_pg), .P3(cla4_1_pg), .C1(clu4_1_c1), .C3(clu4_1_c3),
    .G0(cla4_4_gg), .G1(cla4_3_gg), .G2(cla4_2_gg), .G3(cla4_1_gg), .C2(clu4_1_c2), .C0(C0), .Pg(Pg), .Gg(Gg));  // open: C4
  CLA4 cla4_3 (.X(X[7:4]), .F(S[7:4]), .Y(Y[7:4]), .Pg(cla4_3_pg), .Cin(clu4_1_c1), .Gg(cla4_3_gg));  // open: Cout
  CLA4 cla4_4 (.X(X[3:0]), .F(S[3:0]), .Y(Y[3:0]), .Pg(cla4_4_pg), .Cin(C0), .Gg(cla4_4_gg));  // open: Cout
  // Probe on X
  // Probe on Y
  // Probe on S

  // Notes on the sheet:
  //   Y: pull=down
  //   C0: pull=down
  //   X: pull=down
  //   输入引脚区
  //   请勿修改引脚名称、电路名称及电路封装外观
  //   提示：使用4位先行进位加法器和CLU子电路实现16位并行加法器
  //   功能说明:16位Adder  S=X+Y，C16为最高位进位位，C0为进位输入， Pg、Gg为成组进位生成传递函数
  //   输出引脚区
  //   +
  //   =
  //   无符号加法
endmodule

module CLA4 (
  input  [3:0] X,
  input  [3:0] Y,
  input  Cin,
  output [3:0] F,
  output Cout,
  output Pg,
  output Gg
);

  wire clu4_1_c1, clu4_1_c2, clu4_1_c3, fa_1_g, fa_1_p, fa_2_g, fa_2_p, fa_3_g, fa_3_p, fa_4_g, fa_4_p;

  Hex_Digit_Display hex_digit_display_1 (.value(X));  // open: dp
  FA fa_1 (.A(X[3]), .F(F[3]), .B(Y[3]), .P(fa_1_p), .Cin(clu4_1_c3), .G(fa_1_g));
  Hex_Digit_Display hex_digit_display_2 (.value(Y));  // open: dp
  FA fa_2 (.A(X[2]), .F(F[2]), .B(Y[2]), .P(fa_2_p), .Cin(clu4_1_c2), .G(fa_2_g));
  Hex_Digit_Display hex_digit_display_3 (.value(F));  // open: dp
  CLU4 clu4_1 (
    .P0(fa_4_p), .P1(fa_3_p), .P2(fa_2_p), .P3(fa_1_p), .C1(clu4_1_c1), .C3(clu4_1_c3), .G0(fa_4_g),
    .G1(fa_3_g), .G2(fa_2_g), .G3(fa_1_g), .C2(clu4_1_c2), .C4(Cout), .C0(Cin), .Pg(Pg), .Gg(Gg));
  FA fa_3 (.A(X[1]), .F(F[1]), .B(Y[1]), .P(fa_3_p), .Cin(clu4_1_c1), .G(fa_3_g));
  FA fa_4 (.A(X[0]), .F(F[0]), .B(Y[0]), .P(fa_4_p), .Cin(Cin), .G(fa_4_g));

  // Other names for the same wires on the sheet: Z[3:0] = F

  // Notes on the sheet:
  //   +
  //   =
  //   输出
  //   输入
  //   请勿修改引脚名称、电路名称及电路封装外观
  //   提示：使用全加器和CLU子电路实现四位先行进位加法器CLA4
endmodule

module CLU4 (
  input  P0,
  input  P1,
  input  P2,
  input  P3,
  input  G0,
  input  G1,
  input  G2,
  input  G3,
  input  C0,
  output C1,
  output C3,
  output C2,
  output C4,
  output Pg,
  output Gg
);

  wire and_1_out, and_2_out, and_3_out, and_4_out, and_5_out, and_7_out, and_8_out, and_9_out, and_10_out,
       and_11_out, and_12_out, and_13_out, and_14_out;

  or or_1 (C4, G3, and_1_out, and_2_out, and_3_out, and_4_out);
  and and_1 (and_1_out, P3, G2);
  and and_2 (and_2_out, P3, G1, P2);
  and and_3 (and_3_out, P3, G0, P2, P1);
  and and_4 (and_4_out, P3, P2, P1, P0, C0);
  or or_2 (C3, G2, and_5_out, and_7_out, and_8_out);
  and and_5 (and_5_out, G1, P2);
  and and_6 (Pg, P3, P2, P1, P0);
  and and_7 (and_7_out, G0, P2, P1);
  and and_8 (and_8_out, P2, P1, P0, C0);
  or or_3 (C2, G1, and_9_out, and_10_out);
  and and_9 (and_9_out, G0, P1);
  and and_10 (and_10_out, P1, P0, C0);
  or or_4 (C1, G0, and_11_out);
  and and_11 (and_11_out, P0, C0);
  and and_12 (and_12_out, P3, G2);
  and and_13 (and_13_out, P3, P2, G1);
  and and_14 (and_14_out, P3, P2, P1, G0);
  or or_5 (Gg, G3, and_12_out, and_13_out, and_14_out);

  // Notes on the sheet:
  //   输入引脚
  //   请勿修改引脚名称、电路名称及电路封装外观
  //   提示：使用逻辑门电路实现4位四位先行进位部件CLU，Pg、Gg为成组进位生成传递函数
  //   输出引脚
endmodule

module FA (
  input  A,
  input  B,
  input  Cin,
  output F,
  output P,
  output G
);

  wire xor_1_out;

  xor xor_1 (xor_1_out, A, B);
  and and_1 (G, A, B);
  or or_1 (P, A, B);
  xor xor_2 (F, xor_1_out, Cin);

  // Notes on the sheet:
  //   输入引脚
  //   请勿修改引脚名称、电路名称及电路封装外观
  //   输出引脚
endmodule
