// Logisim project 4-1MUX.circ as structural Verilog: 1 circuit, main circuit main
module main (
  input  I0,
  input  I1,
  input  I2,
  input  I3,
  input  S0,
  input  S1,
  output out_7
);

  wire and_1_out, and_2_out, and_3_out, and_4_out;

  and and_1 (and_1_out, I0, ~S0, ~S1);  // AND_Gate
  and and_2 (and_2_out, I1, ~S0, S1);  // AND_Gate
  and and_3 (and_3_out, I2, S0, ~S1);  // AND_Gate
  and and_4 (and_4_out, I3, S0, S1);
  or or_1 (out_7, and_1_out, and_2_out, and_3_out, and_4_out);
endmodule
