// Logisim project 奇偶校验位.circ as structural Verilog: 1 circuit, main circuit main
module main (
  input  B3,
  input  B2,
  input  B1,
  input  B0,
  output out_5
);

  ExactlyOne xor_1 (.out(out_5), .in0(B3), .in1(B2), .in2(B1), .in3(B0));
endmodule
