// Logisim project 带标志位加法器.circ as structural Verilog: 2 circuits, main circuit main
module main (
  input  [3:0] X,
  input  [3:0] Y,
  input  Cin,
  output [3:0] F,
  output Cout,
  output \零标志ZF ,
  output \符号标志SF ,
  output \进位标志CF ,
  output \溢出标志OF 
);

  wire FA0_cout, FA1_cout, FA2_cout, xor_1_out, xor_2_out, xor_3_out, xor_4_out;

  Hex_Digit_Display hex_digit_display_1 (.value(X));  // open: dp
  xor xor_1 (xor_1_out, Cin, Y[0]);
  Hex_Digit_Display hex_digit_display_2 (.value(Y));  // open: dp
  FA FA0 (.A(X[0]), .B(xor_1_out), .Cin(Cin), .Cout(FA0_cout), .F(F[0]));
  Hex_Digit_Display hex_digit_display_3 (.value(F));  // open: dp
  FA FA1 (.A(X[1]), .B(xor_2_out), .Cin(FA0_cout), .Cout(FA1_cout), .F(F[1]));
  xor xor_2 (xor_2_out, Cin, Y[1]);
  FA FA2 (.A(X[2]), .B(xor_3_out), .Cin(FA1_cout), .Cout(FA2_cout), .F(F[2]));
  xor xor_3 (xor_3_out, Cin, Y[2]);
  xor xor_4 (xor_4_out, Y[3], Cin);
  FA FA3 (.A(X[3]), .B(xor_4_out), .Cin(FA2_cout), .Cout(Cout), .F(F[3]));
  xor xor_5 (\溢出标志OF , Cout, FA2_cout);
  nor nor_1 (\零标志ZF , F[0], F[1], F[2], F[3]);

  assign \符号标志SF  = F[3];
  assign \进位标志CF  = Cout;

  // Other names for the same wires on the sheet: 操作数x[3:0] = X; 操作数y[3:0] = Y; SUM[3:0] = F

  // Notes on the sheet:
  //   输入引脚
  //   +\-
  //   =
  //   请勿修改引脚名称、电路名称及电路封装外观
  //   提示：使用独立逻辑门及全加器FA子电路实现4位二进制数加减法器，禁止直接使用加减法器组件。
  //   输出引脚
endmodule

module FA (
  input  A,
  input  B,
  input  Cin,
  output F,
  output Cout
);

  wire and_1_out, and_2_out, and_3_out;

  xor xor_1 (F, A, B, Cin);
  and and_1 (and_1_out, A, B);
  and and_2 (and_2_out, B, Cin);
  and and_3 (and_3_out, A, Cin);
  or or_1 (Cout, and_1_out, and_2_out, and_3_out);

  // Notes on the sheet:
  //   全加器
endmodule
